// Logisim project PipeLine_forwardLW,SW_Entrega.circ as structural Verilog: 25 circuits, main circuit main
// Zero
module main (
  output R,
  output addi,
  output jump,
  output Load_lw,
  output store_sw,
  output beq
);

  wire alu_1_zero, AluSrc, and_1_out, Branch, Clock, enaPC, ExMem_RegWrite, f_dir, id_ex_1_branch_2,
       id_ex_1_jump_2, id_ex_1_memwrite_2, id_ex_1_regwriteexit, ID_EX__memRead, IF_ID__memWrite, jump_t,
       mem_wr_1_memread_2, MEME_WB_RegWrite, memRead, MemWrite, multiplexer_3_out, multiplexer_5_out,
       not_1_out, not_2_out, RegDest, RegDest2, regWrite, Reset, Stall, Zero;
  wire [1:0] AluOP, Fa, Fb, unidad_de_control_1_aluop;
  wire [3:0] alu_udc_1_operation, salidadisplay_1_s1, salidadisplay_1_s2, salidadisplay_2_s1,
       salidadisplay_2_s2, salidadisplay_3_s1, salidadisplay_3_s2, salidadisplay_4_s1, salidadisplay_4_s2;
  wire [4:0] ExMem_rd, id_ex_1_rd_2, ID_EX__rt_rd, ID_Ex_rs, ID_Ex_rt, MEM_Wb_rd, rd, rs, rt;
  wire [5:0] dedodificador_1_funct, id_ex_1_function_2, opcode;
  wire [6:0] multiplexer_4_out, salidadisplay_1_co1_1, salidadisplay_1_co1_2, salidadisplay_1_co1_3,
       salidadisplay_1_co2_1, salidadisplay_1_co2_2, salidadisplay_1_co2_3, salidadisplay_1_co3_1,
       salidadisplay_1_co3_2, salidadisplay_1_co3_3, salidadisplay_1_co4_1, salidadisplay_1_co4_2,
       salidadisplay_1_co4_3, salidadisplay_1_co5_1, salidadisplay_1_co5_2, salidadisplay_1_co5_3,
       salidadisplay_2_co1_1, salidadisplay_2_co1_2, salidadisplay_2_co1_3, salidadisplay_2_co2_1,
       salidadisplay_2_co2_2, salidadisplay_2_co2_3, salidadisplay_2_co3_1, salidadisplay_2_co3_2,
       salidadisplay_2_co3_3, salidadisplay_2_co4_1, salidadisplay_2_co4_2, salidadisplay_2_co4_3,
       salidadisplay_2_co5_1, salidadisplay_2_co5_2, salidadisplay_2_co5_3, salidadisplay_3_co1_1,
       salidadisplay_3_co1_2, salidadisplay_3_co1_3, salidadisplay_3_co2_1, salidadisplay_3_co2_2,
       salidadisplay_3_co2_3, salidadisplay_3_co3_1, salidadisplay_3_co3_2, salidadisplay_3_co3_3,
       salidadisplay_3_co4_1, salidadisplay_3_co4_2, salidadisplay_3_co4_3, salidadisplay_3_co5_1,
       salidadisplay_3_co5_2, salidadisplay_3_co5_3, salidadisplay_4_co1_1, salidadisplay_4_co1_2,
       salidadisplay_4_co1_3, salidadisplay_4_co2_1, salidadisplay_4_co2_2, salidadisplay_4_co2_3,
       salidadisplay_4_co3_1, salidadisplay_4_co3_2, salidadisplay_4_co3_3, salidadisplay_4_co4_1,
       salidadisplay_4_co4_2, salidadisplay_4_co4_3, salidadisplay_4_co5_1, salidadisplay_4_co5_2,
       salidadisplay_4_co5_3, unidad_de_control_1_alusrc;
  wire [15:0] dedodificador_1_immediate_offset, id_ex_1_inm16_2;
  wire [23:0] bit_extender_1_out, bit_extender_4_out;
  wire [25:0] jumpinf;
  wire [31:0] alu_1_result, Bexit, bit_extender_2_out, bit_extender_3_out, branch_1_branchexit, E_M_r,
       ex_mem_1_pc_1_2, ex_mem_1_r_rt_2, id_ex_1_busa, id_ex_1_busb, id_ex_1_pc_1_2, ID_EX__Instr,
       if_id_1_s_pc_1, IF_ID__Instr, IFINAL, ins2, ins3, ins4, ins5, m_w_r, mem_wr_1_alu_result,
       mem_wr_1_memorydata_2, multiplexer_1_out, multiplexer_2_out, multiplexer_6_out, multiplexer_8_out,
       multiplexer_9_out, multiplexer_10_out, PC2, PC3, PC5, pC_1, pc_1Provi, PC_q, ram_1_data, ram_2_data,
       registros_de_memoria_1_r_rs, registros_de_memoria_1_r_rt;

  Register #(.width(32), .trigger("falling")) PC (
    .D(multiplexer_2_out), .en(enaPC), .Q(PC_q), .clk(Clock), .clr(Reset));
  Bit_Extender #(.in_width(32), .out_width(24)) bit_extender_1 (.in(PC_q), .out(bit_extender_1_out));
  Clock clock_1 (.out(Clock));
  Button button_1 (.out(Reset));
  Debugger debugger_1 (.op(opcode), .R(R), .addi(addi), .jump(jump), .Load_lw(Load_lw), .store_sw(store_sw), .beq(beq));
  Multiplexer #(.width(32)) multiplexer_1 (
    .in0(pc_1Provi), .in1(Bexit), .out(multiplexer_1_out), .sel(and_1_out));  // open: en
  and and_1 (and_1_out, Branch, Zero);
  assign bit_extender_2_out = {{6{1'b0}}, jumpinf};  // Bit_Extender bit_extender_2
  Adder #(.width(32)) adder_1 (.a(32'h1), .b(PC_q), .out(pc_1Provi));  // open: cin, cout
  Multiplexer #(.width(32)) multiplexer_2 (
    .in0(multiplexer_1_out), .in1(bit_extender_2_out), .out(multiplexer_2_out), .sel(jump_t));  // open: en
  RAM #(.addrWidth(24), .dataWidth(32)) ram_1 (
    .addr(bit_extender_1_out), .data(ram_1_data));  // open: sel, clk, ld, clr
  IF_ID if_id_1 (
    .PC_1(pc_1Provi), .Instruccion(ram_1_data), .Clk(Clock), .S_PC_1(if_id_1_s_pc_1),
    .S_Instruccion(IF_ID__Instr), .reset(Reset), .Stall(Stall), .instr0S(ins2), .Pcs(PC2));
  Dedodificador dedodificador_1 (
    .Entrada_Instruccion(IF_ID__Instr), .op(opcode), .rs(rs), .rt(rt), .rd(rd),
    .funct(dedodificador_1_funct), .Jump(jumpinf), .Immediate_offset(dedodificador_1_immediate_offset));  // open: shampt
  Unidad_de_Control unidad_de_control_1 (
    .opcode(opcode), .RegDts(RegDest), .Alusrc(unidad_de_control_1_alusrc[0]), .RegWrite(regWrite),
    .MemREAD(unidad_de_control_1_alusrc[1]), .MenWrite(IF_ID__memWrite),
    .Branch(unidad_de_control_1_alusrc[3]), .AluOP(unidad_de_control_1_aluop),
    .Jump(unidad_de_control_1_alusrc[6]));  // open: Rformat, MemtoRead, lw, sw, beq, Addi
  DotMatrix dotmatrix_1 (
    .col0(salidadisplay_1_co1_1), .col1(salidadisplay_1_co2_1), .col2(salidadisplay_1_co3_1),
    .col3(salidadisplay_1_co4_1), .col4(salidadisplay_1_co5_1));
  DotMatrix dotmatrix_2 (
    .col0(salidadisplay_1_co1_2), .col1(salidadisplay_1_co2_2), .col2(salidadisplay_1_co3_2),
    .col3(salidadisplay_1_co4_2), .col4(salidadisplay_1_co5_2));
  SalidaDisplay salidadisplay_1 (
    .Instruccion(ins2), .PC_1(PC2), .s2(salidadisplay_1_s2), .s1(salidadisplay_1_s1),
    .co1_1(salidadisplay_1_co1_1), .co2_1(salidadisplay_1_co2_1), .co3_1(salidadisplay_1_co3_1),
    .co4_1(salidadisplay_1_co4_1), .co5_1(salidadisplay_1_co5_1), .co5_2(salidadisplay_1_co5_2),
    .co5_3(salidadisplay_1_co5_3), .co4_2(salidadisplay_1_co4_2), .co4_3(salidadisplay_1_co4_3),
    .co3_2(salidadisplay_1_co3_2), .co3_3(salidadisplay_1_co3_3), .co2_2(salidadisplay_1_co2_2),
    .co2_3(salidadisplay_1_co2_3), .co1_2(salidadisplay_1_co1_2), .co1_3(salidadisplay_1_co1_3));
  Multiplexer multiplexer_3 (.in0(regWrite), .in1(1'b0), .out(multiplexer_3_out), .sel(Stall));  // open: en
  DotMatrix dotmatrix_3 (
    .col0(salidadisplay_1_co1_3), .col1(salidadisplay_1_co2_3), .col2(salidadisplay_1_co3_3),
    .col3(salidadisplay_1_co4_3), .col4(salidadisplay_1_co5_3));
  // Probe on Fa
  Forward_Unit forward_unit_1 (
    .EX_MEM__RegWrite(ExMem_RegWrite), .EX_MEM__Rd(ExMem_rd), .ID_EX__rs(ID_Ex_rs), .ID_EX__rt(ID_Ex_rt),
    .MEM_WB___RegWrite(MEME_WB_RegWrite), .MEM_WB_rd(MEM_Wb_rd), .ForwardA(Fa), .ForwardB(Fb),
    .EX_MEM__memWrite(MemWrite), .memForward(f_dir));
  LED led_1 (.in(f_dir));
  Multiplexer #(.width(7)) multiplexer_4 (
    .in0({unidad_de_control_1_alusrc[6], unidad_de_control_1_aluop, unidad_de_control_1_alusrc[3], IF_ID__memWrite, unidad_de_control_1_alusrc[1:0]}),
    .in1({7{1'b0}}), .out(multiplexer_4_out), .sel(Stall));  // open: en
  Multiplexer multiplexer_5 (.in0(RegDest), .in1(1'b0), .out(multiplexer_5_out), .sel(Stall));  // open: en
  Registros_de_memoria registros_de_memoria_1 (
    .R_rs(registros_de_memoria_1_r_rs), .R_rt(registros_de_memoria_1_r_rt), .rt(rt), .rs(rs), .ck(Clock),
    .Dato(m_w_r), .Rw(MEM_Wb_rd), .reset(Reset), .RegWrite(MEME_WB_RegWrite));
  Hex_Digit_Display hex_digit_display_1 (.value(salidadisplay_1_s1));  // open: dp
  Hex_Digit_Display hex_digit_display_2 (.value(salidadisplay_1_s2));  // open: dp
  // Probe on Fb
  ID_EX id_ex_1 (
    .Clock(Clock), .PC_1(if_id_1_s_pc_1), .R_rs(registros_de_memoria_1_r_rs),
    .R_rt(registros_de_memoria_1_r_rt), .Inm16(dedodificador_1_immediate_offset), .Instruction(IF_ID__Instr),
    .BusA(id_ex_1_busa), .BusB(id_ex_1_busb), .Inm16_2(id_ex_1_inm16_2), .Instruction_2(ID_EX__Instr),
    .\function (dedodificador_1_funct), .function_2(id_ex_1_function_2), .RegWrite(multiplexer_3_out),
    .RegWriteExit(id_ex_1_regwriteexit), .reset(Reset), .AluSRC(multiplexer_4_out[0]), .AluSRC_2(AluSrc),
    .MemRead(multiplexer_4_out[1]), .MemRead_2(ID_EX__memRead), .MemWrite(multiplexer_4_out[2]),
    .MemWrite_2(id_ex_1_memwrite_2), .Branch(multiplexer_4_out[3]), .Branch_2(id_ex_1_branch_2),
    .AluOp(multiplexer_4_out[5:4]), .AluOp_2(AluOP), .Jump(multiplexer_4_out[6]), .Jump_2(id_ex_1_jump_2),
    .Rt(rt), .Rt_2(ID_Ex_rt), .Rd(rd), .Rd_2(id_ex_1_rd_2), .Rs(rs), .Rs_2(ID_Ex_rs), .Stall(1'b0),
    .PC_1_2(id_ex_1_pc_1_2), .instSal(ins3), .PcSal(PC3), .RegDest(multiplexer_5_out), .RegDest_2(RegDest2));  // open: rwE, rws
  assign bit_extender_3_out = {{16{1'b0}}, id_ex_1_inm16_2};  // Bit_Extender bit_extender_3
  DotMatrix dotmatrix_4 (
    .col0(salidadisplay_2_co1_1), .col1(salidadisplay_2_co2_1), .col2(salidadisplay_2_co3_1),
    .col3(salidadisplay_2_co4_1), .col4(salidadisplay_2_co5_1));
  SalidaDisplay salidadisplay_2 (
    .Instruccion(ins3), .PC_1(PC3), .s2(salidadisplay_2_s2), .s1(salidadisplay_2_s1),
    .co1_1(salidadisplay_2_co1_1), .co2_1(salidadisplay_2_co2_1), .co3_1(salidadisplay_2_co3_1),
    .co4_1(salidadisplay_2_co4_1), .co5_1(salidadisplay_2_co5_1), .co5_2(salidadisplay_2_co5_2),
    .co5_3(salidadisplay_2_co5_3), .co4_2(salidadisplay_2_co4_2), .co4_3(salidadisplay_2_co4_3),
    .co3_2(salidadisplay_2_co3_2), .co3_3(salidadisplay_2_co3_3), .co2_2(salidadisplay_2_co2_2),
    .co2_3(salidadisplay_2_co2_3), .co1_2(salidadisplay_2_co1_2), .co1_3(salidadisplay_2_co1_3));
  HazardWithForward hazardwithforward_1 (
    .ID_EX__MemRead(ID_EX__memRead), .ID_EX__rt(ID_Ex_rt), .IF_ID__rs(rs), .IF_ID__rt(rt),
    .lw_instruction(IF_ID__memWrite), .PC_enable(enaPC), .Stall_Control(Stall));  // open: IF_ID__stall
  Branch branch_1 (.PC_1(id_ex_1_pc_1_2), .Imm16(id_ex_1_inm16_2), .BranchExit(branch_1_branchexit));
  Multiplexer #(.select(2), .width(32)) multiplexer_6 (
    .in0(id_ex_1_busb), .in1(m_w_r), .in2(E_M_r), .out(multiplexer_6_out), .sel(Fb));  // open: in3, en
  Multiplexer #(.width(5)) multiplexer_7 (
    .in0(ID_Ex_rt), .in1(id_ex_1_rd_2), .out(ID_EX__rt_rd), .sel(RegDest2));  // open: en
  DotMatrix dotmatrix_5 (
    .col0(salidadisplay_2_co1_2), .col1(salidadisplay_2_co2_2), .col2(salidadisplay_2_co3_2),
    .col3(salidadisplay_2_co4_2), .col4(salidadisplay_2_co5_2));
  Multiplexer #(.width(32)) multiplexer_8 (
    .in0(multiplexer_6_out), .in1(bit_extender_3_out), .out(multiplexer_8_out), .sel(AluSrc));  // open: en
  Hex_Digit_Display hex_digit_display_3 (.value(salidadisplay_2_s1));  // open: dp
  DotMatrix dotmatrix_6 (
    .col0(salidadisplay_2_co1_3), .col1(salidadisplay_2_co2_3), .col2(salidadisplay_2_co3_3),
    .col3(salidadisplay_2_co4_3), .col4(salidadisplay_2_co5_3));
  Multiplexer #(.select(2), .width(32)) multiplexer_9 (
    .in0(id_ex_1_busa), .in1(m_w_r), .in2(E_M_r), .out(multiplexer_9_out), .sel(Fa));  // open: in3, en
  Hex_Digit_Display hex_digit_display_4 (.value(salidadisplay_2_s2));  // open: dp
  ALU_UDC alu_udc_1 (.ALUop(AluOP), .Fuction(id_ex_1_function_2), .Operation(alu_udc_1_operation));
  ALU alu_1 (
    .BusA(multiplexer_9_out), .BusB(multiplexer_8_out), .Operation(alu_udc_1_operation),
    .result(alu_1_result), .Zero(alu_1_zero));
  DotMatrix dotmatrix_7 (
    .col0(salidadisplay_3_co1_1), .col1(salidadisplay_3_co2_1), .col2(salidadisplay_3_co3_1),
    .col3(salidadisplay_3_co4_1), .col4(salidadisplay_3_co5_1));
  EX_MEM ex_mem_1 (
    .BranchExit(branch_1_branchexit), .PC_1(id_ex_1_pc_1_2), .R_rt(multiplexer_6_out), .Zero(alu_1_zero),
    .Alu_result(alu_1_result), .Instrucciones(ID_EX__Instr), .Clock(Clock), .BranchExit_2(Bexit),
    .PC_1_2(ex_mem_1_pc_1_2), .R_rt_2(ex_mem_1_r_rt_2), .Zero_2(Zero), .AluResult(E_M_r),
    .Instrucciones_2(ins5), .RegWrite(id_ex_1_regwriteexit), .RegWriteSalida(ExMem_RegWrite), .reset(Reset),
    .rwE(ID_EX__rt_rd), .rwS(ExMem_rd), .MemRead(ID_EX__memRead), .MemRead_2(memRead),
    .MemWrite(id_ex_1_memwrite_2), .MemWrite_2(MemWrite), .Branch(id_ex_1_branch_2), .Branch_2(Branch),
    .Jump(id_ex_1_jump_2), .Jump_2(jump_t), .instSal(ins4), .PCsal(pC_1));  // open: rt, rt_2, rd, rd_2, rs, rs_2
  DotMatrix dotmatrix_8 (
    .col0(salidadisplay_3_co1_2), .col1(salidadisplay_3_co2_2), .col2(salidadisplay_3_co3_2),
    .col3(salidadisplay_3_co4_2), .col4(salidadisplay_3_co5_2));
  SalidaDisplay salidadisplay_3 (
    .Instruccion(ins4), .PC_1(pC_1), .s2(salidadisplay_3_s2), .s1(salidadisplay_3_s1),
    .co1_1(salidadisplay_3_co1_1), .co2_1(salidadisplay_3_co2_1), .co3_1(salidadisplay_3_co3_1),
    .co4_1(salidadisplay_3_co4_1), .co5_1(salidadisplay_3_co5_1), .co5_2(salidadisplay_3_co5_2),
    .co5_3(salidadisplay_3_co5_3), .co4_2(salidadisplay_3_co4_2), .co4_3(salidadisplay_3_co4_3),
    .co3_2(salidadisplay_3_co3_2), .co3_3(salidadisplay_3_co3_3), .co2_2(salidadisplay_3_co2_2),
    .co2_3(salidadisplay_3_co2_3), .co1_2(salidadisplay_3_co1_2), .co1_3(salidadisplay_3_co1_3));
  Multiplexer #(.width(32)) multiplexer_10 (
    .in0(ex_mem_1_r_rt_2), .in1(m_w_r), .out(multiplexer_10_out), .sel(f_dir));  // open: en
  Bit_Extender #(.in_width(32), .out_width(24)) bit_extender_4 (.in(E_M_r), .out(bit_extender_4_out));
  DotMatrix dotmatrix_9 (
    .col0(salidadisplay_3_co1_3), .col1(salidadisplay_3_co2_3), .col2(salidadisplay_3_co3_3),
    .col3(salidadisplay_3_co4_3), .col4(salidadisplay_3_co5_3));
  // Probe on bit_extender_4_out
  Hex_Digit_Display hex_digit_display_5 (.value(salidadisplay_3_s2));  // open: dp
  Hex_Digit_Display hex_digit_display_6 (.value(salidadisplay_3_s1));  // open: dp
  not not_1 (not_1_out, Clock);
  DotMatrix dotmatrix_10 (
    .col0(salidadisplay_4_co1_1), .col1(salidadisplay_4_co2_1), .col2(salidadisplay_4_co3_1),
    .col3(salidadisplay_4_co4_1), .col4(salidadisplay_4_co5_1));
  SalidaDisplay salidadisplay_4 (
    .Instruccion(ins5), .PC_1(PC5), .s2(salidadisplay_4_s2), .s1(salidadisplay_4_s1),
    .co1_1(salidadisplay_4_co1_1), .co2_1(salidadisplay_4_co2_1), .co3_1(salidadisplay_4_co3_1),
    .co4_1(salidadisplay_4_co4_1), .co5_1(salidadisplay_4_co5_1), .co5_2(salidadisplay_4_co5_2),
    .co5_3(salidadisplay_4_co5_3), .co4_2(salidadisplay_4_co4_2), .co4_3(salidadisplay_4_co4_3),
    .co3_2(salidadisplay_4_co3_2), .co3_3(salidadisplay_4_co3_3), .co2_2(salidadisplay_4_co2_2),
    .co2_3(salidadisplay_4_co2_3), .co1_2(salidadisplay_4_co1_2), .co1_3(salidadisplay_4_co1_3));
  RAM #(.addrWidth(24), .dataWidth(32), .bus("separate")) ram_2 (
    .addr(bit_extender_4_out), .din(multiplexer_10_out), .data(ram_2_data), .str(MemWrite), .clk(not_1_out),
    .ld(memRead), .clr(Reset));  // open: sel
  DotMatrix dotmatrix_11 (
    .col0(salidadisplay_4_co1_2), .col1(salidadisplay_4_co2_2), .col2(salidadisplay_4_co3_2),
    .col3(salidadisplay_4_co4_2), .col4(salidadisplay_4_co5_2));
  Mem_Wr mem_wr_1 (
    .clk(Clock), .MemoryData(ram_2_data), .AluResult(E_M_r), .MemoryData_2(mem_wr_1_memorydata_2),
    .Alu_result(mem_wr_1_alu_result), .RegWrite(ExMem_RegWrite), .RegWrite_salida(MEME_WB_RegWrite),
    .reset(Reset), .rwE(ExMem_rd), .rwS(MEM_Wb_rd), .MemRead(memRead), .MemRead_2(mem_wr_1_memread_2),
    .Instruccion(ins5), .PC_1(ex_mem_1_pc_1_2), .Spc_1(IFINAL), .PCsal(PC5));  // open: rt, rt_2, rd, rd_2, rs, rs_2, Sinstru, instsal
  not not_2 (not_2_out, mem_wr_1_memread_2);
  Hex_Digit_Display hex_digit_display_7 (.value(salidadisplay_4_s1));  // open: dp
  DotMatrix dotmatrix_12 (
    .col0(salidadisplay_4_co1_3), .col1(salidadisplay_4_co2_3), .col2(salidadisplay_4_co3_3),
    .col3(salidadisplay_4_co4_3), .col4(salidadisplay_4_co5_3));
  Multiplexer #(.width(32)) multiplexer_11 (
    .in0(mem_wr_1_memorydata_2), .in1(mem_wr_1_alu_result), .out(m_w_r), .sel(not_2_out));  // open: en
  Hex_Digit_Display hex_digit_display_8 (.value(salidadisplay_4_s2));  // open: dp

  // Notes on the sheet:
  //   Camero, Zambrano, Santiago
  //   IF/ID
  //   PC+1
  //   ID/EX
  //   PC+1
  //   EX/MEM
  //   PC+1
  //   EX/MEM
  //   PC+1
endmodule

module Branch (
  input  [31:0] PC_1,
  input  [15:0] Imm16,
  output [31:0] BranchExit
);

  wire [31:0] adder_1_out, bit_extender_1_out, subtractor_1_out;

  assign bit_extender_1_out = {{17{1'b0}}, Imm16[14:0]};  // Bit_Extender bit_extender_1
  Adder #(.width(32)) adder_1 (.a(PC_1), .b(bit_extender_1_out), .out(adder_1_out));  // open: cin, cout
  Subtractor #(.width(32)) subtractor_1 (.a(PC_1), .b(bit_extender_1_out), .out(subtractor_1_out));  // open: bin, bout
  Multiplexer #(.width(32)) multiplexer_1 (
    .in0(adder_1_out), .in1(subtractor_1_out), .out(BranchExit), .sel(Imm16[15]));  // open: en
endmodule

module PC (
  input  [31:0] Entrada_pc_1,
  input  in_2
);

  wire clock_1_out;
  wire [31:0] adder_1_out, multiplexer_1_out, register_1_q;

  Multiplexer #(.width(32)) multiplexer_1 (
    .in0({32{1'b0}}), .in1(adder_1_out), .out(multiplexer_1_out), .sel(in_2));  // open: en
  Adder #(.width(32)) adder_1 (.a(register_1_q), .b(Entrada_pc_1), .out(adder_1_out));  // open: cin, cout
  Register #(.width(32)) register_1 (.D(multiplexer_1_out), .Q(register_1_q), .clk(clock_1_out));  // open: en, clr
  Clock clock_1 (.out(clock_1_out));
  // Probe on register_1_q
endmodule

// Decodificador
module Dedodificador (
  input  [31:0] Entrada_Instruccion,
  output [5:0] op,
  output [4:0] rs,
  output [4:0] rt,
  output [4:0] rd,
  output [4:0] shampt,
  output [5:0] funct,
  output [25:0] Jump,
  output [15:0] Immediate_offset
);


  assign funct = Entrada_Instruccion[5:0];
  assign Immediate_offset = Entrada_Instruccion[15:0];
  assign Jump = Entrada_Instruccion[25:0];
  assign op = Entrada_Instruccion[31:26];
  assign rd = Entrada_Instruccion[15:11];
  assign rs = Entrada_Instruccion[25:21];
  assign rt = Entrada_Instruccion[20:16];
  assign shampt = Entrada_Instruccion[10:6];

  // Notes on the sheet:
  //   Instruccion tipo R
endmodule

module Debugger (
  input  [5:0] op,
  output R,
  output addi,
  output jump,
  output Load_lw,
  output store_sw,
  output beq
);

  // Probe on op
  Comparator #(.width(6)) comparator_1 (.a(op), .b({6{1'b0}}), .eq(R));  // open: gt, lt
  Comparator #(.width(6)) comparator_2 (.a(op), .b(6'b001000), .eq(addi));  // open: gt, lt
  Comparator #(.width(6)) comparator_3 (.a(op), .b(6'b000010), .eq(jump));  // open: gt, lt
  Comparator #(.width(6)) comparator_4 (.a(op), .b(6'b100011), .eq(Load_lw));  // open: gt, lt
  Comparator #(.width(6)) comparator_5 (.a(op), .b(6'b101011), .eq(store_sw));  // open: gt, lt
  Comparator #(.width(6)) comparator_6 (.a(op), .b(6'b000100), .eq(beq));  // open: gt, lt
endmodule

// RM
module Registros_de_memoria (
  input  ck,
  input  RegWrite,
  input  [31:0] Dato,
  input  [4:0] rs,
  input  [4:0] rt,
  input  reset,
  input  [4:0] Rw,
  output [31:0] R_rs,
  output [31:0] R_rt
);

  wire _0b, _1b, _2b, _3b, _4b, _5b, _6b, _7b, _8b, _9b, _10b, _11b, _12b, _13b, _14b, _15b, _16b, _17b,
       _18b, _19b, _20b, _21b, _22b, _23b, _24b, _25b, _26b, _27b, _28b, _29b, _30b, _31b, decoder_1_out0,
       decoder_1_out1, decoder_1_out2, decoder_1_out3, decoder_1_out4, decoder_1_out5, decoder_1_out6,
       decoder_1_out7, decoder_1_out8, decoder_1_out9, decoder_1_out10, decoder_1_out11, decoder_1_out12,
       decoder_1_out13, decoder_1_out14, decoder_1_out15, decoder_1_out16, decoder_1_out17, decoder_1_out18,
       decoder_1_out19, decoder_1_out20, decoder_1_out21, decoder_1_out22, decoder_1_out23, decoder_1_out24,
       decoder_1_out25, decoder_1_out26, decoder_1_out27, decoder_1_out28, decoder_1_out29, decoder_1_out30,
       decoder_1_out31;
  wire [31:0] _0, _1, _2, _3, _4, _5, _6, _7, _8, _9, _10, _11, _12, _13, _14, _15, _16, _17, _18, _19, _20,
       _21, _22, _23, _24, _25, _26, _27, _28, _29, _30, _31;

  Register #(.width(32)) u__0 (.D(Dato), .en(_0b), .Q(_0), .clk(ck), .clr(reset));
  Register #(.width(32)) u__1 (.D(Dato), .en(_1b), .Q(_1), .clk(ck), .clr(reset));
  Register #(.width(32)) u__2 (.D(Dato), .en(_2b), .Q(_2), .clk(ck), .clr(reset));
  Register #(.width(32)) u__3 (.D(Dato), .en(_3b), .Q(_3), .clk(ck), .clr(reset));
  Register #(.width(32)) u__4 (.D(Dato), .en(_4b), .Q(_4), .clk(ck), .clr(reset));
  Register #(.width(32)) u__5 (.D(Dato), .en(_5b), .Q(_5), .clk(ck), .clr(reset));
  Register #(.width(32)) u__6 (.D(Dato), .en(_6b), .Q(_6), .clk(ck), .clr(reset));
  Register #(.width(32)) u__7 (.D(Dato), .en(_7b), .Q(_7), .clk(ck), .clr(reset));
  Register #(.width(32)) u__8 (.D(Dato), .en(_8b), .Q(_8), .clk(ck), .clr(reset));
  Register #(.width(32)) u__9 (.D(Dato), .en(_9b), .Q(_9), .clk(ck), .clr(reset));
  Register #(.width(32)) u__10 (.D(Dato), .en(_10b), .Q(_10), .clk(ck), .clr(reset));
  Register #(.width(32)) u__11 (.D(Dato), .en(_11b), .Q(_11), .clk(ck), .clr(reset));
  Register #(.width(32)) u__12 (.D(Dato), .en(_12b), .Q(_12), .clk(ck), .clr(reset));
  Register #(.width(32)) u__13 (.D(Dato), .en(_13b), .Q(_13), .clk(ck), .clr(reset));
  Register #(.width(32)) u__14 (.D(Dato), .en(_14b), .Q(_14), .clk(ck), .clr(reset));
  Register #(.width(32)) u__15 (.D(Dato), .en(_15b), .Q(_15), .clk(ck), .clr(reset));
  Register #(.width(32)) u__16 (.D(Dato), .en(_16b), .Q(_16), .clk(ck), .clr(reset));
  Register #(.width(32)) u__17 (.D(Dato), .en(_17b), .Q(_17), .clk(ck), .clr(reset));
  Register #(.width(32)) u__18 (.D(Dato), .en(_18b), .Q(_18), .clk(ck), .clr(reset));
  Register #(.width(32)) u__19 (.D(Dato), .en(_19b), .Q(_19), .clk(ck), .clr(reset));
  Register #(.width(32)) u__20 (.D(Dato), .en(_20b), .Q(_20), .clk(ck), .clr(reset));
  Register #(.width(32)) u__21 (.D(Dato), .en(_21b), .Q(_21), .clk(ck), .clr(reset));
  Register #(.width(32)) u__22 (.D(Dato), .en(_22b), .Q(_22), .clk(ck), .clr(reset));
  Register #(.width(32)) u__23 (.D(Dato), .en(_23b), .Q(_23), .clk(ck), .clr(reset));
  Register #(.width(32)) u__24 (.D(Dato), .en(_24b), .Q(_24), .clk(ck), .clr(reset));
  Register #(.width(32)) u__25 (.D(Dato), .en(_25b), .Q(_25), .clk(ck), .clr(reset));
  Register #(.width(32)) u__26 (.D(Dato), .en(_26b), .Q(_26), .clk(ck), .clr(reset));
  Register #(.width(32)) u__27 (.D(Dato), .en(_27b), .Q(_27), .clk(ck), .clr(reset));
  Register #(.width(32)) u__28 (.D(Dato), .en(_28b), .Q(_28), .clk(ck), .clr(reset));
  Register #(.width(32)) u__29 (.D(Dato), .en(_29b), .Q(_29), .clk(ck), .clr(reset));
  Register #(.width(32)) u__30 (.D(Dato), .en(_30b), .Q(_30), .clk(ck), .clr(reset));
  Register #(.width(32)) u__31 (.D(Dato), .en(_31b), .Q(_31), .clk(ck), .clr(reset));
  and and_1 (_0b, decoder_1_out0, RegWrite);
  and and_2 (_1b, decoder_1_out1, RegWrite);
  and and_3 (_2b, decoder_1_out2, RegWrite);
  and and_4 (_3b, decoder_1_out3, RegWrite);
  and and_5 (_4b, decoder_1_out4, RegWrite);
  and and_6 (_5b, decoder_1_out5, RegWrite);
  and and_7 (_6b, decoder_1_out6, RegWrite);
  and and_8 (_7b, decoder_1_out7, RegWrite);
  and and_9 (_8b, decoder_1_out8, RegWrite);
  and and_10 (_9b, decoder_1_out9, RegWrite);
  and and_11 (_10b, decoder_1_out10, RegWrite);
  and and_12 (_11b, decoder_1_out11, RegWrite);
  and and_13 (_12b, decoder_1_out12, RegWrite);
  and and_14 (_13b, decoder_1_out13, RegWrite);
  and and_15 (_14b, decoder_1_out14, RegWrite);
  and and_16 (_15b, decoder_1_out15, RegWrite);
  and and_17 (_16b, decoder_1_out16, RegWrite);
  and and_18 (_17b, decoder_1_out17, RegWrite);
  and and_19 (_18b, decoder_1_out18, RegWrite);
  and and_20 (_19b, decoder_1_out19, RegWrite);
  and and_21 (_20b, decoder_1_out20, RegWrite);
  and and_22 (_21b, decoder_1_out21, RegWrite);
  and and_23 (_22b, decoder_1_out22, RegWrite);
  and and_24 (_23b, decoder_1_out23, RegWrite);
  and and_25 (_24b, decoder_1_out24, RegWrite);
  and and_26 (_25b, decoder_1_out25, RegWrite);
  and and_27 (_26b, decoder_1_out26, RegWrite);
  and and_28 (_27b, decoder_1_out27, RegWrite);
  and and_29 (_28b, decoder_1_out28, RegWrite);
  and and_30 (_29b, decoder_1_out29, RegWrite);
  and and_31 (_30b, decoder_1_out30, RegWrite);
  and and_32 (_31b, decoder_1_out31, RegWrite);
  Multiplexer #(.select(5), .width(32)) multiplexer_1 (
    .in0(_0), .in1(_1), .in2(_2), .in3(_3), .in4(_4), .in5(_5), .in6(_6), .in7(_7), .in8(_8), .in9(_9),
    .in10(_10), .in11(_11), .in12(_12), .in13(_13), .in14(_14), .in15(_15), .in16(_16), .in17(_17),
    .in18(_18), .in19(_19), .in20(_20), .in21(_21), .in22(_22), .in23(_23), .in24(_24), .in25(_25),
    .in26(_26), .in27(_27), .in28(_28), .in29(_29), .in30(_30), .in31(_31), .out(R_rs), .sel(rs));  // open: en
  // Probe on rs
  Multiplexer #(.select(5), .width(32)) multiplexer_2 (
    .in0(_0), .in1(_1), .in2(_2), .in3(_3), .in4(_4), .in5(_5), .in6(_6), .in7(_7), .in8(_8), .in9(_9),
    .in10(_10), .in11(_11), .in12(_12), .in13(_13), .in14(_14), .in15(_15), .in16(_16), .in17(_17),
    .in18(_18), .in19(_19), .in20(_20), .in21(_21), .in22(_22), .in23(_23), .in24(_24), .in25(_25),
    .in26(_26), .in27(_27), .in28(_28), .in29(_29), .in30(_30), .in31(_31), .out(R_rt), .sel(rt));  // open: en
  Decoder #(.select(5)) decoder_1 (
    .out0(decoder_1_out0), .out1(decoder_1_out1), .out2(decoder_1_out2), .out3(decoder_1_out3),
    .out4(decoder_1_out4), .out5(decoder_1_out5), .out6(decoder_1_out6), .out7(decoder_1_out7),
    .out8(decoder_1_out8), .out9(decoder_1_out9), .out10(decoder_1_out10), .out11(decoder_1_out11),
    .out12(decoder_1_out12), .out13(decoder_1_out13), .out14(decoder_1_out14), .out15(decoder_1_out15),
    .out16(decoder_1_out16), .out17(decoder_1_out17), .out18(decoder_1_out18), .out19(decoder_1_out19),
    .out20(decoder_1_out20), .out21(decoder_1_out21), .out22(decoder_1_out22), .out23(decoder_1_out23),
    .out24(decoder_1_out24), .out25(decoder_1_out25), .out26(decoder_1_out26), .out27(decoder_1_out27),
    .out28(decoder_1_out28), .out29(decoder_1_out29), .out30(decoder_1_out30), .out31(decoder_1_out31),
    .sel(Rw));  // open: en

  // Other names for the same wires on the sheet: R = reset; RW_t = RegWrite

  // Notes on the sheet:
  //   RS
  //   RT
endmodule

module MiniUnidadDeControl (
  input  [5:0] opcode,
  output out_2
);

  wire comparator_1_eq;

  Comparator #(.width(6)) comparator_1 (.a(opcode), .b({6{1'b0}}), .eq(comparator_1_eq));  // open: gt, lt
  not not_1 (out_2, comparator_1_eq);

  // Notes on the sheet:
  //   0= add / 1 = addi
endmodule

// UControl
module UDC (
  input  [5:0] Opcode,
  output TipoR,
  output addi,
  output lw,
  output sw,
  output beq,
  output j
);

  wire not_1_out, not_2_out, not_3_out, not_4_out, not_5_out, not_6_out, not_7_out, not_8_out, not_9_out,
       not_10_out, not_11_out, not_12_out, not_13_out, not_14_out, not_15_out, not_16_out, not_17_out,
       not_18_out, not_19_out, not_20_out, not_21_out, not_22_out, not_23_out, not_24_out, not_25_out,
       not_26_out;

  not not_1 (not_1_out, Opcode[5]);
  not not_2 (not_2_out, Opcode[4]);
  not not_3 (not_3_out, Opcode[3]);
  not not_4 (not_4_out, Opcode[2]);
  not not_5 (not_5_out, Opcode[1]);
  not not_6 (not_6_out, Opcode[0]);
  not not_7 (not_7_out, Opcode[5]);
  not not_8 (not_8_out, Opcode[4]);
  not not_9 (not_9_out, Opcode[2]);
  not not_10 (not_10_out, Opcode[1]);
  not not_11 (not_11_out, Opcode[0]);
  not not_12 (not_12_out, Opcode[4]);
  not not_13 (not_13_out, Opcode[3]);
  not not_14 (not_14_out, Opcode[2]);
  not not_15 (not_15_out, Opcode[4]);
  not not_16 (not_16_out, Opcode[2]);
  not not_17 (not_17_out, Opcode[5]);
  not not_18 (not_18_out, Opcode[4]);
  not not_19 (not_19_out, Opcode[3]);
  not not_20 (not_20_out, Opcode[1]);
  not not_21 (not_21_out, Opcode[0]);
  not not_22 (not_22_out, Opcode[5]);
  not not_23 (not_23_out, Opcode[4]);
  not not_24 (not_24_out, Opcode[3]);
  not not_25 (not_25_out, Opcode[2]);
  not not_26 (not_26_out, Opcode[0]);
  and and_1 (TipoR, not_1_out, not_2_out, not_3_out, not_4_out, not_5_out, not_6_out);
  and and_2 (addi, not_7_out, not_8_out, Opcode[3], not_9_out, not_10_out, not_11_out);
  and and_3 (lw, Opcode[5], not_12_out, not_13_out, not_14_out, Opcode[1], Opcode[0]);
  and and_4 (sw, Opcode[5], not_15_out, Opcode[3], not_16_out, Opcode[1], Opcode[0]);
  and and_5 (beq, not_17_out, not_18_out, not_19_out, Opcode[2], not_20_out, not_21_out);
  and and_6 (j, not_22_out, not_23_out, not_24_out, not_25_out, Opcode[1], not_26_out);
endmodule

module ALU (
  input  [31:0] BusA,
  input  [31:0] BusB,
  input  [3:0] Operation,
  output [31:0] result,
  output Zero
);

  wire [1:0] aritmeticaalu_1_dir;
  wire [31:0] add, \and , \or , subs;

  Adder #(.width(32)) adder_1 (.a(BusA), .b(BusB), .out(add));  // open: cin, cout
  Subtractor #(.width(32)) subtractor_1 (.a(BusA), .b(BusB), .out(subs));  // open: bin, bout
  aritmeticaALU aritmeticaalu_1 (.operation(Operation), .dir(aritmeticaalu_1_dir));
  assign \and  = BusA & BusB;  // AND_Gate and_1, 32 bits wide
  assign \or  = BusA | BusB;  // OR_Gate or_1, 32 bits wide
  Multiplexer #(.select(2), .width(32)) multiplexer_1 (
    .in0(add), .in1(subs), .in2(\and ), .in3(\or ), .out(result), .sel(aritmeticaalu_1_dir));  // open: en
  Comparator #(.width(32)) comparator_1 (.a(result), .b({32{1'b0}}), .eq(Zero));  // open: gt, lt

  // Notes on the sheet:
  //   0000 and / 0001 or/ 0010 suma / 0110 resta
endmodule

// UCALU
module ALU_UDC (
  input  [1:0] ALUop,
  input  [5:0] Fuction,
  output [3:0] Operation
);

  wire and_2_out, and_3_out, and_4_out, not_1_out, not_2_out;

  and and_1 (Operation[3], ALUop[1], ALUop[0]);
  and and_2 (and_2_out, ALUop[1], Fuction[1]);
  not not_1 (not_1_out, ALUop[1]);
  not not_2 (not_2_out, Fuction[2]);
  and and_3 (and_3_out, ALUop[1], Fuction[0]);
  and and_4 (and_4_out, ALUop[1], Fuction[3]);
  or or_1 (Operation[2], ALUop[0], and_2_out);
  or or_2 (Operation[1], not_1_out, not_2_out);
  or or_3 (Operation[0], and_3_out, and_4_out);

  // Notes on the sheet:
  //   00 lw/sw/addi
endmodule

module Data_Memory (
  input  Clock,
  input  [23:0] Address,
  input  [31:0] Write_Data,
  input  memory_write,
  input  memory_read,
  input  reset,
  output [31:0] Read_Data
);

  RAM #(.addrWidth(24), .dataWidth(32), .bus("separate")) ram_1 (
    .addr(Address), .din(Write_Data), .data(Read_Data), .str(memory_write), .clk(Clock), .ld(memory_read),
    .clr(reset));  // open: sel

  // Other names for the same wires on the sheet: ck = Clock
endmodule

module Unidad_de_Control (
  input  [5:0] opcode,
  output RegDts,
  output Rformat,
  output Alusrc,
  output MemtoRead,
  output lw,
  output RegWrite,
  output MemREAD,
  output sw,
  output MenWrite,
  output Branch,
  output beq,
  output Addi,
  output [1:0] AluOP,
  output Jump
);

  wire and_6_out, and_7_out, and_8_out, and_9_out, and_10_out, and_12_out, and_14_out, not_1_out, not_2_out,
       not_3_out, not_4_out, not_5_out, not_6_out, not_7_out, not_8_out, not_9_out, not_10_out, not_11_out,
       not_12_out, not_13_out, not_14_out, not_15_out, not_16_out, not_17_out, not_18_out, not_19_out,
       not_20_out, not_21_out, not_22_out, not_23_out, not_24_out, not_25_out, not_26_out, not_27_out,
       not_28_out, not_29_out, not_30_out, not_31_out, not_32_out, not_33_out, not_34_out, not_35_out,
       not_36_out, not_37_out, not_38_out, not_39_out, not_40_out, not_41_out, not_42_out, not_43_out,
       not_44_out, not_45_out, not_46_out, not_47_out, not_48_out, not_49_out, not_50_out, not_51_out,
       not_52_out, not_53_out, not_54_out, not_55_out, not_56_out, not_57_out, not_58_out, not_59_out,
       or_1_out, or_2_out, or_3_out, or_4_out;
  wire [1:0] and_18_out, and_19_out, bit_extender_1_out, bit_extender_2_out, bit_extender_3_out, or_7_out,
       or_8_out;

  Comparator #(.width(6)) comparator_1 (.a(opcode), .b(6'b000010), .eq(Jump));  // open: gt, lt
  not not_1 (not_1_out, opcode[5]);
  not not_2 (not_2_out, opcode[4]);
  not not_3 (not_3_out, opcode[3]);
  and and_1 (Rformat, not_1_out, not_2_out, not_3_out, not_4_out, not_5_out, not_6_out);
  not not_4 (not_4_out, opcode[2]);
  not not_5 (not_5_out, opcode[1]);
  not not_6 (not_6_out, opcode[0]);
  not not_7 (not_7_out, opcode[4]);
  not not_8 (not_8_out, opcode[3]);
  and and_2 (lw, opcode[5], not_7_out, not_8_out, not_9_out, opcode[1], opcode[0]);
  not not_9 (not_9_out, opcode[2]);
  not not_10 (not_10_out, opcode[4]);
  and and_3 (sw, opcode[5], not_10_out, opcode[3], not_11_out, opcode[1], opcode[0]);
  not not_11 (not_11_out, opcode[2]);
  not not_12 (not_12_out, opcode[5]);
  not not_13 (not_13_out, opcode[4]);
  not not_14 (not_14_out, opcode[3]);
  and and_4 (beq, not_12_out, not_13_out, not_14_out, opcode[2], not_15_out, not_16_out);
  not not_15 (not_15_out, opcode[1]);
  not not_16 (not_16_out, opcode[0]);
  not not_17 (not_17_out, opcode[5]);
  not not_18 (not_18_out, opcode[4]);
  and and_5 (Addi, not_17_out, not_18_out, opcode[3], not_19_out, not_20_out, not_21_out);
  not not_19 (not_19_out, opcode[2]);
  not not_20 (not_20_out, opcode[1]);
  not not_21 (not_21_out, opcode[0]);
  not not_22 (not_22_out, lw);
  and and_6 (and_6_out, Rformat, not_22_out, not_23_out, not_24_out, not_25_out);
  not not_23 (not_23_out, sw);
  not not_24 (not_24_out, beq);
  not not_25 (not_25_out, Addi);
  not not_26 (not_26_out, Rformat);
  and and_7 (and_7_out, not_26_out, lw, not_27_out, not_28_out, not_29_out);
  not not_27 (not_27_out, sw);
  not not_28 (not_28_out, beq);
  not not_29 (not_29_out, Addi);
  not not_30 (not_30_out, Rformat);
  not not_31 (not_31_out, lw);
  and and_8 (and_8_out, not_30_out, not_31_out, sw, not_32_out, not_33_out);
  not not_32 (not_32_out, beq);
  not not_33 (not_33_out, Addi);
  not not_34 (not_34_out, Rformat);
  not not_35 (not_35_out, lw);
  and and_9 (and_9_out, not_34_out, not_35_out, not_36_out, beq, not_37_out);
  not not_36 (not_36_out, sw);
  not not_37 (not_37_out, Addi);
  not not_38 (not_38_out, Rformat);
  not not_39 (not_39_out, lw);
  and and_10 (and_10_out, not_38_out, not_39_out, not_40_out, not_41_out, Addi);
  not not_40 (not_40_out, sw);
  not not_41 (not_41_out, beq);
  not not_42 (not_42_out, and_7_out);
  not not_43 (not_43_out, and_8_out);
  and and_11 (RegDts, and_6_out, not_42_out, not_43_out, not_44_out, not_45_out);
  not not_44 (not_44_out, and_9_out);
  not not_45 (not_45_out, and_10_out);
  not not_46 (not_46_out, and_6_out);
  or or_1 (or_1_out, and_7_out, and_8_out);
  not not_47 (not_47_out, and_9_out);
  not not_48 (not_48_out, and_6_out);
  or or_2 (or_2_out, and_6_out, and_7_out);
  not not_49 (not_49_out, or_3_out);
  or or_3 (or_3_out, and_8_out, and_9_out);
  not not_50 (not_50_out, and_6_out);
  not not_51 (not_51_out, and_8_out);
  not not_52 (not_52_out, and_9_out);
  not not_53 (not_53_out, and_6_out);
  not not_54 (not_54_out, and_7_out);
  not not_55 (not_55_out, and_9_out);
  not not_56 (not_56_out, and_6_out);
  not not_57 (not_57_out, and_7_out);
  not not_58 (not_58_out, and_8_out);
  or or_4 (or_4_out, and_7_out, and_8_out);
  and and_12 (and_12_out, not_46_out, or_1_out, not_47_out);
  and and_13 (MemtoRead, not_48_out, and_7_out);
  and and_14 (and_14_out, or_2_out, not_49_out);
  or or_5 (RegWrite, and_14_out, Addi);
  and and_15 (MemREAD, not_50_out, and_7_out, not_51_out, not_52_out);
  and and_16 (MenWrite, not_53_out, not_54_out, and_8_out, not_55_out);
  and and_17 (Branch, not_56_out, not_57_out, not_58_out, and_9_out);
  assign bit_extender_1_out = {{1{1'b1}}, 1'b1};  // Bit_Extender bit_extender_1
  assign bit_extender_2_out = {{1{1'b0}}, and_9_out};  // Bit_Extender bit_extender_2
  not not_59 (not_59_out, or_4_out);
  or or_6 (Alusrc, and_12_out, Addi);
  assign bit_extender_3_out = {{1{1'b0}}, not_59_out};  // Bit_Extender bit_extender_3
  assign and_18_out = bit_extender_2_out & bit_extender_3_out;  // AND_Gate and_18, 2 bits wide
  assign or_7_out = bit_extender_1_out | and_18_out;  // OR_Gate or_7, 2 bits wide
  assign or_8_out = bit_extender_2_out | and_18_out;  // OR_Gate or_8, 2 bits wide
  assign and_19_out = or_7_out & or_8_out;  // AND_Gate and_19, 2 bits wide
  Multiplexer #(.width(2)) multiplexer_1 (.in0(and_19_out), .in1(2'b10), .out(AluOP), .sel(Rformat));  // open: en
endmodule

module aritmeticaALU (
  input  [3:0] operation,
  output [1:0] dir
);

  not not_1 (dir[1], operation[1]);
  or or_1 (dir[0], operation[0], operation[2]);

  // Notes on the sheet:
  //   0000 and / 0001 or/ 0010 suma / 0110 resta
  //   00 suma / 01 resta / 10 and / 11 or
endmodule

module IF_ID (
  input  Clk,
  input  Stall,
  input  [31:0] PC_1,
  input  [31:0] Instruccion,
  input  reset,
  output [31:0] Pcs,
  output [31:0] S_PC_1,
  output [31:0] S_Instruccion,
  output [31:0] instr0S
);

  wire not_1_out;

  not not_1 (not_1_out, Stall);
  Register #(.width(32), .trigger("falling")) register_1 (.D(PC_1), .en(not_1_out), .Q(S_PC_1), .clk(Clk), .clr(reset));
  Register #(.width(32), .trigger("falling")) register_2 (
    .D(Instruccion), .en(not_1_out), .Q(S_Instruccion), .clk(Clk), .clr(reset));

  assign instr0S = Instruccion;
  assign Pcs = PC_1;
endmodule

// DEBUG
module SalidaDisplay (
  input  [31:0] Instruccion,
  input  [31:0] PC_1,
  output [3:0] s1,
  output [6:0] co1_1,
  output [6:0] co1_2,
  output [6:0] co1_3,
  output [3:0] s2,
  output [6:0] co2_1,
  output [6:0] co2_2,
  output [6:0] co2_3,
  output [6:0] co3_1,
  output [6:0] co3_2,
  output [6:0] co3_3,
  output [6:0] co4_1,
  output [6:0] co4_2,
  output [6:0] co4_3,
  output [6:0] co5_1,
  output [6:0] co5_2,
  output [6:0] co5_3
);

  wire and_1_out, and_2_out, and_3_out, and_4_out, and_5_out, and_6_out, and_7_out, and_8_out, and_9_out,
       and_10_out, and_11_out, and_12_out, and_13_out, and_14_out, and_15_out, and_16_out, and_17_out,
       and_18_out, and_19_out, and_20_out, and_21_out, and_22_out, and_23_out, and_24_out, and_25_out,
       and_26_out, and_27_out, and_28_out, and_29_out, and_30_out, and_31_out, and_32_out, and_33_out,
       and_34_out, and_35_out, and_36_out, and_37_out, and_38_out, and_39_out, and_40_out, and_41_out,
       and_42_out, and_43_out, and_44_out, and_45_out, and_46_out, and_47_out, and_48_out, and_49_out,
       and_50_out, and_51_out, and_52_out, and_53_out, and_54_out, and_55_out, and_56_out, and_57_out,
       and_58_out, and_59_out, and_60_out, and_61_out, and_62_out, and_63_out, b0, b1, b2, b3, b4, b5, b6,
       b7, not_1_out, not_2_out, not_3_out, not_4_out, not_5_out, not_6_out, not_7_out, not_8_out, not_9_out,
       not_10_out, not_11_out, not_12_out, not_13_out, not_14_out, not_15_out, not_16_out, not_17_out,
       not_18_out, not_19_out, not_20_out, not_21_out, not_22_out, not_23_out, not_24_out, not_25_out,
       not_26_out, not_27_out, not_28_out, not_29_out, not_30_out, not_31_out, not_32_out, not_33_out,
       not_34_out, not_35_out, not_36_out, not_37_out, not_38_out, not_39_out, not_40_out, not_41_out,
       not_42_out, not_43_out, not_44_out, not_45_out, not_46_out, not_47_out, not_48_out, not_49_out,
       not_50_out, not_51_out, not_52_out, not_53_out, not_54_out, not_55_out, not_56_out, not_57_out,
       not_58_out, not_59_out, not_60_out, not_61_out, not_62_out, not_63_out, not_64_out, not_65_out,
       not_66_out, not_67_out, not_68_out, not_69_out, not_70_out, not_71_out, not_72_out, not_73_out,
       not_74_out, not_75_out, not_76_out, not_77_out, not_78_out, not_79_out, not_80_out, not_81_out,
       not_82_out, not_83_out, not_84_out, not_85_out, not_86_out, not_87_out, not_88_out, not_89_out,
       not_90_out, not_91_out, not_92_out, not_93_out, not_94_out, not_95_out, not_96_out, not_97_out,
       not_98_out, not_99_out, not_100_out, not_101_out, not_102_out, not_103_out, not_104_out, not_105_out,
       not_106_out, not_107_out, not_108_out, not_109_out, not_110_out, not_111_out, not_112_out,
       not_113_out, not_114_out, not_115_out, not_116_out, not_117_out, not_118_out, not_119_out,
       not_120_out, not_121_out, zero;
  wire [1:0] unidad_de_control_1_aluop;
  wire [3:0] alu_udc_1_operation, Dir, seleccionadormatrix_1_direccion;
  wire [5:0] dedodificador_1_funct, dedodificador_1_op;

  Dedodificador dedodificador_1 (
    .Entrada_Instruccion(Instruccion), .op(dedodificador_1_op), .funct(dedodificador_1_funct));  // open: rs, rt, rd, shampt, Jump, Immediate_offset
  Debugger debugger_1 (.op(dedodificador_1_op), .R(b5), .addi(b4), .jump(b1), .Load_lw(b3), .store_sw(b2), .beq(b0));
  Comparator #(.width(32)) comparator_1 (.a(Instruccion), .b({32{1'b0}}), .eq(zero));  // open: gt, lt
  Unidad_de_Control unidad_de_control_1 (
    .opcode(dedodificador_1_op), .AluOP(unidad_de_control_1_aluop));  // open: RegDts, Rformat, Alusrc, MemtoRead, lw, RegWrite, MemREAD, sw, MenWrite, Branch, beq, Addi, Jump
  ALU_UDC alu_udc_1 (
    .ALUop(unidad_de_control_1_aluop), .Fuction(dedodificador_1_funct), .Operation(alu_udc_1_operation));
  aritmeticaALU aritmeticaalu_1 (.operation(alu_udc_1_operation), .dir({b7, b6}));
  seleccionadorMatrix seleccionadormatrix_1 (
    .Entrada({b7, b6, b5, b4, b3, b2, b1, b0}), .Direccion(seleccionadormatrix_1_direccion));
  Multiplexer #(.width(4)) multiplexer_1 (
    .in0(seleccionadormatrix_1_direccion), .in1(4'b0000), .out(Dir), .sel(zero));  // open: en
  DotMatrix dotmatrix_1 (.col0({7{1'b1}}), .col1(7'b0100000), .col2(7'b0010000), .col3(7'b0001000), .col4({7{1'b1}}));
  DotMatrix dotmatrix_2 (.col0({7{1'b1}}), .col1(7'b1000001), .col2(7'b1000001), .col3(7'b1000001), .col4({7{1'b1}}));
  DotMatrix dotmatrix_3 (.col0({7{1'b1}}), .col1(7'b1001000), .col2(7'b1001000), .col3(7'b1001000), .col4(7'b1111000));
  DotMatrix dotmatrix_4 (.col0({7{1'b1}}), .col1(7'b1001000), .col2(7'b1001100), .col3(7'b1001010), .col4(7'b1111001));
  Multiplexer #(.select(4), .width(7)) multiplexer_2 (
    .in0({7{1'b1}}), .in1({7{1'b1}}), .in2(7'b1111001), .in3({7{1'b1}}), .in4({7{1'b1}}), .in5({7{1'b1}}),
    .in6({7{1'b1}}), .in7(7'b1111001), .in8(7'b1000011), .in9({7{1'b1}}), .out(co1_1), .sel(Dir));  // open: in10, in11, in12, in13, in14, in15, en
  Multiplexer #(.select(4), .width(7)) multiplexer_3 (
    .in0(7'b0100000), .in1(7'b1001000), .in2(7'b1001001), .in3(7'b1001000), .in4(7'b1000001),
    .in5(7'b1001000), .in6(7'b0000001), .in7(7'b1001001), .in8(7'b1000001), .in9(7'b1001001), .out(co2_1),
    .sel(Dir));  // open: in10, in11, in12, in13, in14, in15, en
  Multiplexer #(.select(4), .width(7)) multiplexer_4 (
    .in0(7'b0010000), .in1(7'b1001000), .in2(7'b1001001), .in3(7'b1001000), .in4(7'b1000001),
    .in5(7'b1001000), .in6(7'b0000001), .in7(7'b1001001), .in8(7'b1000001), .in9(7'b1001001), .out(co3_1),
    .sel(Dir));  // open: in10, in11, in12, in13, in14, in15, en
  Multiplexer #(.select(4), .width(7)) multiplexer_5 (
    .in0(7'b0001000), .in1(7'b1001000), .in2(7'b1001001), .in3(7'b1001000), .in4(7'b1000001),
    .in5(7'b1001000), .in6(7'b0000001), .in7(7'b1001001), .in8(7'b1000001), .in9(7'b1001001), .out(co4_1),
    .sel(Dir));  // open: in10, in11, in12, in13, in14, in15, en
  Multiplexer #(.select(4), .width(7)) multiplexer_6 (
    .in0({7{1'b1}}), .in1({7{1'b1}}), .in2(7'b1001111), .in3({7{1'b1}}), .in4({7{1'b1}}), .in5({7{1'b1}}),
    .in6(7'b0000001), .in7(7'b1001111), .in8({7{1'b1}}), .in9({7{1'b1}}), .out(co5_1), .sel(Dir));  // open: in10, in11, in12, in13, in14, in15, en
  Multiplexer #(.select(4), .width(7)) multiplexer_7 (
    .in0({7{1'b1}}), .in1({7{1'b1}}), .in2({7{1'b1}}), .in3({7{1'b1}}), .in4({7{1'b1}}), .in5({7{1'b1}}),
    .in6({7{1'b1}}), .in7({7{1'b1}}), .in8({7{1'b1}}), .out(co1_2), .sel(Dir));  // open: in9, in10, in11, in12, in13, in14, in15, en
  Multiplexer #(.select(4), .width(7)) multiplexer_8 (
    .in0(7'b1000001), .in1(7'b1000001), .in2(7'b0000001), .in3(7'b0100000), .in4(7'b1001000),
    .in5(7'b1000001), .in6(7'b0000010), .in7(7'b0000010), .in8(7'b0000001), .in9(7'b1001001), .out(co2_2),
    .sel(Dir));  // open: in10, in11, in12, in13, in14, in15, en
  Multiplexer #(.select(4), .width(7)) multiplexer_9 (
    .in0(7'b1000001), .in1(7'b1000001), .in2(7'b0000001), .in3(7'b0010000), .in4(7'b1001100),
    .in5(7'b1000001), .in6(7'b0000100), .in7(7'b0000100), .in8(7'b0000001), .in9(7'b1001001), .out(co3_2),
    .sel(Dir));  // open: in10, in11, in12, in13, in14, in15, en
  Multiplexer #(.select(4), .width(7)) multiplexer_10 (
    .in0(7'b1000001), .in1(7'b1000001), .in2(7'b0000001), .in3(7'b0001000), .in4(7'b1001010),
    .in5(7'b1000001), .in6(7'b0000010), .in7(7'b0000010), .in8(7'b0000001), .in9(7'b1001001), .out(co4_2),
    .sel(Dir));  // open: in10, in11, in12, in13, in14, in15, en
  Multiplexer #(.select(4), .width(7)) multiplexer_11 (
    .in0({7{1'b1}}), .in1({7{1'b1}}), .in2({7{1'b1}}), .in3({7{1'b1}}), .in4(7'b1111001), .in5({7{1'b1}}),
    .in6({7{1'b1}}), .in7({7{1'b1}}), .in8({7{1'b1}}), .in9(7'b1001001), .out(co5_2), .sel(Dir));  // open: in10, in11, in12, in13, in14, in15, en
  Multiplexer #(.select(4), .width(7)) multiplexer_12 (
    .in0({7{1'b1}}), .in1({7{1'b1}}), .in2({7{1'b1}}), .in3({7{1'b1}}), .in4({7{1'b0}}), .in5(7'b1000001),
    .in6({7{1'b0}}), .in7({7{1'b0}}), .in8({7{1'b1}}), .in9(7'b1111000), .out(co1_3), .sel(Dir));  // open: in10, in11, in12, in13, in14, in15, en
  Multiplexer #(.select(4), .width(7)) multiplexer_13 (
    .in0(7'b1001000), .in1(7'b1000001), .in2(7'b1001001), .in3(7'b1000001), .in4({7{1'b0}}),
    .in5(7'b1000001), .in6({7{1'b0}}), .in7({7{1'b0}}), .in8(7'b0100000), .in9(7'b1001000), .out(co2_3),
    .sel(Dir));  // open: in10, in11, in12, in13, in14, in15, en
  Multiplexer #(.select(4), .width(7)) multiplexer_14 (
    .in0(7'b1001000), .in1(7'b1000001), .in2(7'b1001001), .in3(7'b1000001), .in4({7{1'b0}}), .in5({7{1'b1}}),
    .in6({7{1'b0}}), .in7({7{1'b0}}), .in8(7'b0010000), .in9(7'b1001000), .out(co3_3), .sel(Dir));  // open: in10, in11, in12, in13, in14, in15, en
  Multiplexer #(.select(4), .width(7)) multiplexer_15 (
    .in0(7'b1001000), .in1(7'b1000001), .in2(7'b1001001), .in3(7'b1000001), .in4({7{1'b0}}),
    .in5(7'b1000001), .in6({7{1'b0}}), .in7({7{1'b0}}), .in8(7'b0100000), .in9(7'b1001000), .out(co4_3),
    .sel(Dir));  // open: in10, in11, in12, in13, in14, in15, en
  Multiplexer #(.select(4), .width(7)) multiplexer_16 (
    .in0(7'b1111000), .in1({7{1'b1}}), .in2({7{1'b1}}), .in3({7{1'b1}}), .in4({7{1'b0}}), .in5(7'b1000001),
    .in6({7{1'b0}}), .in7({7{1'b0}}), .in8({7{1'b1}}), .in9({7{1'b1}}), .out(co5_3), .sel(Dir));  // open: in10, in11, in12, in13, in14, in15, en
  and and_1 (and_1_out, PC_1[6], PC_1[4], PC_1[3], PC_1[1]);
  and and_2 (and_2_out, PC_1[6], PC_1[4], PC_1[3], PC_1[2]);
  and and_3 (and_3_out, PC_1[6], PC_1[5]);
  not not_1 (not_1_out, PC_1[5]);
  not not_2 (not_2_out, PC_1[4]);
  not not_3 (not_3_out, PC_1[5]);
  not not_4 (not_4_out, PC_1[3]);
  not not_5 (not_5_out, PC_1[2]);
  not not_6 (not_6_out, PC_1[1]);
  not not_7 (not_7_out, PC_1[5]);
  not not_8 (not_8_out, PC_1[3]);
  not not_9 (not_9_out, PC_1[6]);
  not not_10 (not_10_out, PC_1[5]);
  not not_11 (not_11_out, PC_1[6]);
  not not_12 (not_12_out, PC_1[4]);
  not not_13 (not_13_out, PC_1[3]);
  not not_14 (not_14_out, PC_1[5]);
  not not_15 (not_15_out, PC_1[4]);
  not not_16 (not_16_out, PC_1[5]);
  not not_17 (not_17_out, PC_1[3]);
  not not_18 (not_18_out, PC_1[2]);
  not not_19 (not_19_out, PC_1[1]);
  not not_20 (not_20_out, PC_1[5]);
  not not_21 (not_21_out, PC_1[4]);
  not not_22 (not_22_out, PC_1[5]);
  not not_23 (not_23_out, PC_1[4]);
  not not_24 (not_24_out, PC_1[5]);
  not not_25 (not_25_out, PC_1[6]);
  not not_26 (not_26_out, PC_1[5]);
  not not_27 (not_27_out, PC_1[3]);
  not not_28 (not_28_out, PC_1[2]);
  not not_29 (not_29_out, PC_1[4]);
  not not_30 (not_30_out, PC_1[3]);
  not not_31 (not_31_out, PC_1[3]);
  not not_32 (not_32_out, PC_1[3]);
  not not_33 (not_33_out, PC_1[2]);
  not not_34 (not_34_out, PC_1[4]);
  not not_35 (not_35_out, PC_1[4]);
  not not_36 (not_36_out, PC_1[6]);
  not not_37 (not_37_out, PC_1[5]);
  not not_38 (not_38_out, PC_1[4]);
  not not_39 (not_39_out, PC_1[2]);
  not not_40 (not_40_out, PC_1[1]);
  not not_41 (not_41_out, PC_1[6]);
  not not_42 (not_42_out, PC_1[5]);
  not not_43 (not_43_out, PC_1[3]);
  not not_44 (not_44_out, PC_1[2]);
  not not_45 (not_45_out, PC_1[6]);
  not not_46 (not_46_out, PC_1[5]);
  not not_47 (not_47_out, PC_1[1]);
  not not_48 (not_48_out, PC_1[4]);
  not not_49 (not_49_out, PC_1[3]);
  not not_50 (not_50_out, PC_1[3]);
  not not_51 (not_51_out, PC_1[2]);
  not not_52 (not_52_out, PC_1[1]);
  not not_53 (not_53_out, PC_1[2]);
  not not_54 (not_54_out, PC_1[4]);
  not not_55 (not_55_out, PC_1[3]);
  not not_56 (not_56_out, PC_1[1]);
  not not_57 (not_57_out, PC_1[4]);
  not not_58 (not_58_out, PC_1[2]);
  not not_59 (not_59_out, PC_1[1]);
  not not_60 (not_60_out, PC_1[6]);
  not not_61 (not_61_out, PC_1[4]);
  not not_62 (not_62_out, PC_1[3]);
  not not_63 (not_63_out, PC_1[1]);
  not not_64 (not_64_out, PC_1[6]);
  not not_65 (not_65_out, PC_1[5]);
  not not_66 (not_66_out, PC_1[4]);
  not not_67 (not_67_out, PC_1[6]);
  not not_68 (not_68_out, PC_1[5]);
  not not_69 (not_69_out, PC_1[2]);
  not not_70 (not_70_out, PC_1[1]);
  not not_71 (not_71_out, PC_1[6]);
  not not_72 (not_72_out, PC_1[5]);
  not not_73 (not_73_out, PC_1[2]);
  not not_74 (not_74_out, PC_1[6]);
  not not_75 (not_75_out, PC_1[4]);
  not not_76 (not_76_out, PC_1[3]);
  not not_77 (not_77_out, PC_1[2]);
  not not_78 (not_78_out, PC_1[4]);
  not not_79 (not_79_out, PC_1[3]);
  not not_80 (not_80_out, PC_1[2]);
  not not_81 (not_81_out, PC_1[1]);
  not not_82 (not_82_out, PC_1[4]);
  not not_83 (not_83_out, PC_1[3]);
  not not_84 (not_84_out, PC_1[2]);
  not not_85 (not_85_out, PC_1[1]);
  not not_86 (not_86_out, PC_1[5]);
  not not_87 (not_87_out, PC_1[4]);
  not not_88 (not_88_out, PC_1[2]);
  not not_89 (not_89_out, PC_1[4]);
  not not_90 (not_90_out, PC_1[1]);
  not not_91 (not_91_out, PC_1[3]);
  not not_92 (not_92_out, PC_1[5]);
  not not_93 (not_93_out, PC_1[4]);
  not not_94 (not_94_out, PC_1[3]);
  not not_95 (not_95_out, PC_1[2]);
  not not_96 (not_96_out, PC_1[6]);
  not not_97 (not_97_out, PC_1[5]);
  not not_98 (not_98_out, PC_1[3]);
  not not_99 (not_99_out, PC_1[5]);
  not not_100 (not_100_out, PC_1[4]);
  not not_101 (not_101_out, PC_1[1]);
  not not_102 (not_102_out, PC_1[6]);
  not not_103 (not_103_out, PC_1[5]);
  not not_104 (not_104_out, PC_1[3]);
  not not_105 (not_105_out, PC_1[2]);
  not not_106 (not_106_out, PC_1[1]);
  not not_107 (not_107_out, PC_1[6]);
  not not_108 (not_108_out, PC_1[5]);
  not not_109 (not_109_out, PC_1[2]);
  not not_110 (not_110_out, PC_1[4]);
  not not_111 (not_111_out, PC_1[3]);
  not not_112 (not_112_out, PC_1[1]);
  not not_113 (not_113_out, PC_1[3]);
  not not_114 (not_114_out, PC_1[1]);
  not not_115 (not_115_out, PC_1[4]);
  not not_116 (not_116_out, PC_1[2]);
  not not_117 (not_117_out, PC_1[1]);
  not not_118 (not_118_out, PC_1[4]);
  not not_119 (not_119_out, PC_1[1]);
  not not_120 (not_120_out, PC_1[1]);
  not not_121 (not_121_out, PC_1[3]);
  or or_1 (s1[3], and_1_out, and_2_out, and_3_out);
  and and_4 (and_4_out, PC_1[5], PC_1[3]);
  and and_5 (and_5_out, PC_1[5], PC_1[4]);
  and and_6 (and_6_out, PC_1[6], not_1_out, not_2_out);
  and and_7 (and_7_out, PC_1[6], not_3_out, not_4_out);
  and and_8 (and_8_out, PC_1[6], PC_1[3], not_5_out, not_6_out);
  and and_9 (and_9_out, not_7_out, PC_1[4], not_8_out, PC_1[2]);
  and and_10 (and_10_out, not_9_out, not_10_out, PC_1[4], PC_1[3]);
  and and_11 (and_11_out, not_11_out, PC_1[5], not_12_out, not_13_out);
  and and_12 (and_12_out, PC_1[5], PC_1[4], PC_1[3], PC_1[2]);
  and and_13 (and_13_out, PC_1[6], not_14_out, not_15_out);
  and and_14 (and_14_out, PC_1[6], not_16_out, not_17_out);
  and and_15 (and_15_out, PC_1[6], PC_1[3], not_18_out, not_19_out);
  and and_16 (and_16_out, not_20_out, not_21_out, PC_1[3], PC_1[1]);
  and and_17 (and_17_out, not_22_out, not_23_out, PC_1[3], PC_1[2]);
  and and_18 (and_18_out, not_24_out, PC_1[3], PC_1[2], PC_1[1]);
  and and_19 (and_19_out, not_25_out, not_26_out, PC_1[4], not_27_out, not_28_out);
  and and_20 (and_20_out, PC_1[5], not_29_out, not_30_out);
  and and_21 (and_21_out, PC_1[5], not_31_out, PC_1[1]);
  and and_22 (and_22_out, PC_1[5], not_32_out, PC_1[2]);
  and and_23 (and_23_out, PC_1[5], PC_1[4], PC_1[3], not_33_out);
  and and_24 (and_24_out, PC_1[6], not_34_out, PC_1[2], PC_1[1]);
  and and_25 (and_25_out, PC_1[6], not_35_out, PC_1[3]);
  and and_26 (and_26_out, PC_1[6], PC_1[3], PC_1[1]);
  and and_27 (and_27_out, PC_1[6], PC_1[3], PC_1[2]);
  and and_28 (and_28_out, not_36_out, not_37_out, not_38_out, PC_1[3], not_39_out, not_40_out);
  and and_29 (and_29_out, not_41_out, not_42_out, PC_1[4], not_43_out, not_44_out, PC_1[1]);
  and and_30 (and_30_out, not_45_out, not_46_out, PC_1[4], PC_1[3], PC_1[2], not_47_out);
  and and_31 (and_31_out, PC_1[5], not_48_out, not_49_out, PC_1[2], PC_1[1]);
  and and_32 (and_32_out, PC_1[5], PC_1[4], not_50_out, not_51_out, not_52_out);
  and and_33 (and_33_out, PC_1[5], PC_1[4], PC_1[3], not_53_out, PC_1[1]);
  and and_34 (and_34_out, PC_1[6], not_54_out, not_55_out, PC_1[2], not_56_out);
  and and_35 (and_35_out, PC_1[6], not_57_out, PC_1[3], PC_1[2], PC_1[1]);
  and and_36 (and_36_out, PC_1[6], PC_1[4], PC_1[3], not_58_out, not_59_out);
  and and_37 (and_37_out, PC_1[6], PC_1[5], PC_1[1]);
  and and_38 (and_38_out, not_60_out, not_61_out, not_62_out, PC_1[2], not_63_out);
  and and_39 (and_39_out, not_64_out, not_65_out, not_66_out, PC_1[2], PC_1[1]);
  and and_40 (and_40_out, not_67_out, not_68_out, PC_1[4], not_69_out, not_70_out);
  and and_41 (and_41_out, not_71_out, not_72_out, PC_1[4], PC_1[3], not_73_out);
  and and_42 (and_42_out, not_74_out, PC_1[5], not_75_out, not_76_out, not_77_out, PC_1[1]);
  and and_43 (and_43_out, PC_1[5], not_78_out, PC_1[3], PC_1[2]);
  and and_44 (and_44_out, PC_1[5], PC_1[4], not_79_out, PC_1[2], PC_1[1]);
  and and_45 (and_45_out, PC_1[5], PC_1[4], PC_1[3], not_80_out, not_81_out);
  and and_46 (and_46_out, PC_1[6], not_82_out, not_83_out, not_84_out, not_85_out);
  and and_47 (and_47_out, PC_1[6], not_86_out, not_87_out, not_88_out, PC_1[1]);
  and and_48 (and_48_out, PC_1[6], not_89_out, PC_1[3], PC_1[2], not_90_out);
  and and_49 (and_49_out, PC_1[6], PC_1[4], not_91_out, PC_1[2]);
  and and_50 (and_50_out, PC_1[6], PC_1[4], PC_1[2], PC_1[1]);
  and and_51 (and_51_out, not_92_out, not_93_out, not_94_out, not_95_out, PC_1[1]);
  and and_52 (and_52_out, not_96_out, not_97_out, not_98_out, PC_1[2], PC_1[1]);
  and and_53 (and_53_out, not_99_out, not_100_out, PC_1[3], PC_1[2], not_101_out);
  and and_54 (and_54_out, not_102_out, not_103_out, PC_1[4], not_104_out, not_105_out, not_106_out);
  and and_55 (and_55_out, not_107_out, not_108_out, PC_1[4], PC_1[3], not_109_out, PC_1[1]);
  and and_56 (and_56_out, PC_1[5], not_110_out, not_111_out, not_112_out);
  and and_57 (and_57_out, PC_1[5], not_113_out, PC_1[2], not_114_out);
  and and_58 (and_58_out, PC_1[5], not_115_out, PC_1[3], PC_1[1]);
  and and_59 (and_59_out, PC_1[5], PC_1[3], PC_1[2], PC_1[1]);
  and and_60 (and_60_out, PC_1[5], PC_1[4], PC_1[3], not_116_out, not_117_out);
  and and_61 (and_61_out, PC_1[6], not_118_out, PC_1[3], not_119_out);
  and and_62 (and_62_out, PC_1[6], PC_1[3], PC_1[2], not_120_out);
  and and_63 (and_63_out, PC_1[6], PC_1[4], not_121_out, PC_1[1]);
  or or_2 (s1[2], and_4_out, and_5_out, and_6_out, and_7_out, and_8_out);
  or or_3 (s1[1], and_9_out, and_10_out, and_11_out, and_12_out, and_13_out, and_14_out, and_15_out);
  or or_4 (s1[0], and_16_out, and_17_out, and_18_out, and_19_out, and_20_out, and_21_out, and_22_out, and_23_out, and_24_out, and_25_out, and_26_out, and_27_out);
  or or_5 (s2[3], and_28_out, and_29_out, and_30_out, and_31_out, and_32_out, and_33_out, and_34_out, and_35_out, and_36_out, and_37_out);
  or or_6 (s2[2], and_38_out, and_39_out, and_40_out, and_41_out, and_42_out, and_43_out, and_44_out, and_45_out, and_46_out, and_47_out, and_48_out, and_49_out, and_50_out);
  or or_7 (s2[1], and_51_out, and_52_out, and_53_out, and_54_out, and_55_out, and_56_out, and_57_out, and_58_out, and_59_out, and_60_out, and_61_out, and_62_out, and_63_out);

  assign s2[0] = PC_1[0];

  // Other names for the same wires on the sheet: f = PC_1[1]; e = PC_1[2]; d = PC_1[3]; c = PC_1[4]; b = PC_1[5];
  //   a = PC_1[6]; salida4 = s1[0]; salida3 = s1[1]; salida2 = s1[2]; salida1 = s1[3]; g = PC_1[0]; salida8 = PC_1[0];
  //   salida7 = s2[1]; salida6 = s2[2]; salida5 = s2[3]

  // Notes on the sheet:
  //   Dir TIpo
  //   Tipo R
  //   Addi
  //   lw
  //   sw
  //   Jump
  //   Branch
endmodule

module ID_EX (
  input  Stall,
  input  Clock,
  input  [31:0] PC_1,
  input  [31:0] R_rs,
  input  [31:0] R_rt,
  input  [5:0] \function ,
  input  [15:0] Inm16,
  input  [31:0] Instruction,
  input  RegWrite,
  input  [4:0] rwE,
  input  reset,
  input  AluSRC,
  input  MemRead,
  input  MemWrite,
  input  Branch,
  input  [1:0] AluOp,
  input  Jump,
  input  [4:0] Rt,
  input  [4:0] Rd,
  input  [4:0] Rs,
  input  RegDest,
  output [31:0] PcSal,
  output [31:0] PC_1_2,
  output [31:0] BusA,
  output [31:0] BusB,
  output [5:0] function_2,
  output [15:0] Inm16_2,
  output [31:0] instSal,
  output [31:0] Instruction_2,
  output RegWriteExit,
  output [4:0] rws,
  output AluSRC_2,
  output MemRead_2,
  output MemWrite_2,
  output Branch_2,
  output [1:0] AluOp_2,
  output Jump_2,
  output [4:0] Rt_2,
  output [4:0] Rd_2,
  output [4:0] Rs_2,
  output RegDest_2
);

  wire multiplexer_7_out, multiplexer_9_out, multiplexer_10_out, multiplexer_11_out, multiplexer_12_out,
       multiplexer_14_out, multiplexer_18_out;
  wire [1:0] multiplexer_13_out;
  wire [4:0] multiplexer_8_out, multiplexer_15_out, multiplexer_16_out, multiplexer_17_out;
  wire [5:0] multiplexer_4_out;
  wire [15:0] multiplexer_5_out;
  wire [31:0] multiplexer_1_out, multiplexer_2_out, multiplexer_3_out, multiplexer_6_out;

  Multiplexer #(.width(32)) multiplexer_1 (
    .in0(PC_1), .in1({32{1'b0}}), .out(multiplexer_1_out), .sel(Stall));  // open: en
  Multiplexer #(.width(32)) multiplexer_2 (
    .in0(R_rs), .in1({32{1'b0}}), .out(multiplexer_2_out), .sel(Stall));  // open: en
  Multiplexer #(.width(32)) multiplexer_3 (
    .in0(R_rt), .in1({32{1'b0}}), .out(multiplexer_3_out), .sel(Stall));  // open: en
  Multiplexer #(.width(6)) multiplexer_4 (
    .in0(\function ), .in1({6{1'b0}}), .out(multiplexer_4_out), .sel(Stall));  // open: en
  Multiplexer #(.width(16)) multiplexer_5 (
    .in0(Inm16), .in1({16{1'b0}}), .out(multiplexer_5_out), .sel(Stall));  // open: en
  Multiplexer #(.width(32)) multiplexer_6 (
    .in0(Instruction), .in1({32{1'b0}}), .out(multiplexer_6_out), .sel(Stall));  // open: en
  Multiplexer multiplexer_7 (.in0(RegWrite), .in1(1'b0), .out(multiplexer_7_out), .sel(Stall));  // open: en
  Multiplexer #(.width(5)) multiplexer_8 (
    .in0(rwE), .in1({5{1'b0}}), .out(multiplexer_8_out), .sel(Stall));  // open: en
  Multiplexer multiplexer_9 (.in0(AluSRC), .in1(1'b0), .out(multiplexer_9_out), .sel(Stall));  // open: en
  Multiplexer multiplexer_10 (.in0(MemRead), .in1(1'b0), .out(multiplexer_10_out), .sel(Stall));  // open: en
  Multiplexer multiplexer_11 (.in0(MemWrite), .in1(1'b0), .out(multiplexer_11_out), .sel(Stall));  // open: en
  Multiplexer multiplexer_12 (.in0(Branch), .in1(1'b0), .out(multiplexer_12_out), .sel(Stall));  // open: en
  Multiplexer #(.width(2)) multiplexer_13 (
    .in0(AluOp), .in1(2'b00), .out(multiplexer_13_out), .sel(Stall));  // open: en
  Multiplexer multiplexer_14 (.in0(Jump), .in1(1'b0), .out(multiplexer_14_out), .sel(Stall));  // open: en
  Multiplexer #(.width(5)) multiplexer_15 (
    .in0(Rt), .in1({5{1'b0}}), .out(multiplexer_15_out), .sel(Stall));  // open: en
  Multiplexer #(.width(5)) multiplexer_16 (
    .in0(Rd), .in1({5{1'b0}}), .out(multiplexer_16_out), .sel(Stall));  // open: en
  Multiplexer #(.width(5)) multiplexer_17 (
    .in0(Rs), .in1({5{1'b0}}), .out(multiplexer_17_out), .sel(Stall));  // open: en
  Multiplexer multiplexer_18 (.in0(RegDest), .in1(1'b0), .out(multiplexer_18_out), .sel(Stall));  // open: en
  Register #(.width(32), .trigger("falling")) register_1 (
    .D(multiplexer_1_out), .Q(PC_1_2), .clk(Clock), .clr(reset));  // open: en
  Register #(.width(32), .trigger("falling")) register_2 (
    .D(multiplexer_2_out), .Q(BusA), .clk(Clock), .clr(reset));  // open: en
  Register #(.width(32), .trigger("falling")) register_3 (
    .D(multiplexer_3_out), .Q(BusB), .clk(Clock), .clr(reset));  // open: en
  Register #(.width(6), .trigger("falling")) register_4 (
    .D(multiplexer_4_out), .Q(function_2), .clk(Clock), .clr(reset));  // open: en
  Register #(.width(16), .trigger("falling")) register_5 (
    .D(multiplexer_5_out), .Q(Inm16_2), .clk(Clock), .clr(reset));  // open: en
  Register #(.width(32), .trigger("falling")) register_6 (
    .D(multiplexer_6_out), .Q(Instruction_2), .clk(Clock), .clr(reset));  // open: en
  Register #(.width(1), .trigger("falling")) register_7 (
    .D(multiplexer_7_out), .Q(RegWriteExit), .clk(Clock), .clr(reset));  // open: en
  Register #(.width(5), .trigger("falling")) register_8 (
    .D(multiplexer_8_out), .Q(rws), .clk(Clock), .clr(reset));  // open: en
  Register #(.width(1), .trigger("falling")) register_9 (
    .D(multiplexer_9_out), .Q(AluSRC_2), .clk(Clock), .clr(reset));  // open: en
  Register #(.width(1), .trigger("falling")) register_10 (
    .D(multiplexer_10_out), .Q(MemRead_2), .clk(Clock), .clr(reset));  // open: en
  Register #(.width(1), .trigger("falling")) register_11 (
    .D(multiplexer_11_out), .Q(MemWrite_2), .clk(Clock), .clr(reset));  // open: en
  Register #(.width(1), .trigger("falling")) register_12 (
    .D(multiplexer_12_out), .Q(Branch_2), .clk(Clock), .clr(reset));  // open: en
  Register #(.width(2), .trigger("falling")) register_13 (
    .D(multiplexer_13_out), .Q(AluOp_2), .clk(Clock), .clr(reset));  // open: en
  Register #(.width(1), .trigger("falling")) register_14 (
    .D(multiplexer_14_out), .Q(Jump_2), .clk(Clock), .clr(reset));  // open: en
  Register #(.width(5), .trigger("falling")) register_15 (
    .D(multiplexer_15_out), .Q(Rt_2), .clk(Clock), .clr(reset));  // open: en
  Register #(.width(5), .trigger("falling")) register_16 (
    .D(multiplexer_16_out), .Q(Rd_2), .clk(Clock), .clr(reset));  // open: en
  Register #(.width(5), .trigger("falling")) register_17 (
    .D(multiplexer_17_out), .Q(Rs_2), .clk(Clock), .clr(reset));  // open: en
  Register #(.width(1), .trigger("falling")) register_18 (
    .D(multiplexer_18_out), .Q(RegDest_2), .clk(Clock), .clr(reset));  // open: en

  assign instSal = Instruction;
  assign PcSal = PC_1;
endmodule

// Ex/Mem
module EX_MEM (
  input  Clock,
  input  [31:0] BranchExit,
  input  [31:0] PC_1,
  input  [31:0] R_rt,
  input  Zero,
  input  [31:0] Alu_result,
  input  [31:0] Instrucciones,
  input  RegWrite,
  input  [4:0] rwE,
  input  reset,
  input  MemRead,
  input  MemWrite,
  input  Branch,
  input  Jump,
  input  [4:0] rt,
  input  [4:0] rd,
  input  [4:0] rs,
  output [31:0] BranchExit_2,
  output [31:0] PCsal,
  output [31:0] PC_1_2,
  output [31:0] R_rt_2,
  output Zero_2,
  output [31:0] AluResult,
  output [31:0] instSal,
  output [31:0] Instrucciones_2,
  output RegWriteSalida,
  output [4:0] rwS,
  output MemRead_2,
  output MemWrite_2,
  output Branch_2,
  output Jump_2,
  output [4:0] rt_2,
  output [4:0] rd_2,
  output [4:0] rs_2
);

  Register #(.width(32), .trigger("falling")) register_1 (
    .D(BranchExit), .Q(BranchExit_2), .clk(Clock), .clr(reset));  // open: en
  Register #(.width(32), .trigger("falling")) register_2 (.D(PC_1), .Q(PC_1_2), .clk(Clock), .clr(reset));  // open: en
  Register #(.width(32), .trigger("falling")) register_3 (.D(R_rt), .Q(R_rt_2), .clk(Clock), .clr(reset));  // open: en
  Register #(.width(1), .trigger("falling")) register_4 (.D(Zero), .Q(Zero_2), .clk(Clock), .clr(reset));  // open: en
  Register #(.width(32), .trigger("falling")) register_5 (
    .D(Alu_result), .Q(AluResult), .clk(Clock), .clr(reset));  // open: en
  Register #(.width(32), .trigger("falling")) register_6 (
    .D(Instrucciones), .Q(Instrucciones_2), .clk(Clock), .clr(reset));  // open: en
  Register #(.width(1), .trigger("falling")) register_7 (
    .D(RegWrite), .Q(RegWriteSalida), .clk(Clock), .clr(reset));  // open: en
  Register #(.width(5), .trigger("falling")) register_8 (.D(rwE), .Q(rwS), .clk(Clock), .clr(reset));  // open: en
  Register #(.width(1), .trigger("falling")) register_9 (
    .D(MemRead), .Q(MemRead_2), .clk(Clock), .clr(reset));  // open: en
  Register #(.width(1), .trigger("falling")) register_10 (
    .D(MemWrite), .Q(MemWrite_2), .clk(Clock), .clr(reset));  // open: en
  Register #(.width(1), .trigger("falling")) register_11 (
    .D(Branch), .Q(Branch_2), .clk(Clock), .clr(reset));  // open: en
  Register #(.width(1), .trigger("falling")) register_12 (.D(Jump), .Q(Jump_2), .clk(Clock), .clr(reset));  // open: en
  Register #(.width(5), .trigger("falling")) register_13 (.D(rt), .Q(rt_2), .clk(Clock), .clr(reset));  // open: en
  Register #(.width(5), .trigger("falling")) register_14 (.D(rd), .Q(rd_2), .clk(Clock), .clr(reset));  // open: en
  Register #(.width(5), .trigger("falling")) register_15 (.D(rs), .Q(rs_2), .clk(Clock), .clr(reset));  // open: en

  assign instSal = Instrucciones;
  assign PCsal = PC_1;
endmodule

// MEM/WR
module Mem_Wr (
  input  clk,
  input  [31:0] MemoryData,
  input  [31:0] AluResult,
  input  RegWrite,
  input  [4:0] rwE,
  input  reset,
  input  MemRead,
  input  [4:0] rt,
  input  [4:0] rd,
  input  [4:0] rs,
  input  [31:0] Instruccion,
  input  [31:0] PC_1,
  output [31:0] MemoryData_2,
  output [31:0] Alu_result,
  output RegWrite_salida,
  output [4:0] rwS,
  output MemRead_2,
  output [4:0] rt_2,
  output [4:0] rd_2,
  output [4:0] rs_2,
  output [31:0] instsal,
  output [31:0] Sinstru,
  output [31:0] Spc_1,
  output [31:0] PCsal
);

  Register #(.width(32), .trigger("falling")) register_1 (
    .D(MemoryData), .Q(MemoryData_2), .clk(clk), .clr(reset));  // open: en
  Register #(.width(32), .trigger("falling")) register_2 (
    .D(AluResult), .Q(Alu_result), .clk(clk), .clr(reset));  // open: en
  Register #(.width(1), .trigger("falling")) register_3 (
    .D(RegWrite), .Q(RegWrite_salida), .clk(clk), .clr(reset));  // open: en
  Register #(.width(5), .trigger("falling")) register_4 (.D(rwE), .Q(rwS), .clk(clk), .clr(reset));  // open: en
  Register #(.width(1), .trigger("falling")) register_5 (
    .D(MemRead), .Q(MemRead_2), .clk(clk), .clr(reset));  // open: en
  Register #(.width(5), .trigger("falling")) register_6 (.D(rt), .Q(rt_2), .clk(clk), .clr(reset));  // open: en
  Register #(.width(5), .trigger("falling")) register_7 (.D(rd), .Q(rd_2), .clk(clk), .clr(reset));  // open: en
  Register #(.width(5), .trigger("falling")) register_8 (.D(rs), .Q(rs_2), .clk(clk), .clr(reset));  // open: en
  Register #(.width(32), .trigger("falling")) register_9 (
    .D(Instruccion), .Q(instsal), .clk(clk), .clr(reset));  // open: en
  Register #(.width(32), .trigger("falling")) register_10 (.D(PC_1), .Q(Spc_1), .clk(clk), .clr(reset));  // open: en

  assign PCsal = PC_1;
  assign Sinstru = instsal;
endmodule

module seleccionadorMatrix (
  input  [7:0] Entrada,
  output [3:0] Direccion
);

  wire and_1_out, and_2_out, and_3_out, and_4_out, and_5_out, and_6_out, and_7_out, and_8_out, and_9_out,
       and_10_out, and_11_out, and_12_out, and_13_out, and_14_out, not_1_out, not_2_out, not_3_out,
       not_4_out, not_5_out, not_6_out, not_7_out, not_8_out, not_9_out, not_10_out, not_11_out, not_12_out,
       not_13_out, not_14_out, not_15_out, not_16_out, not_17_out, not_18_out, not_19_out, not_20_out,
       not_21_out, not_22_out, not_23_out, not_24_out;

  not not_1 (not_1_out, Entrada[5]);
  not not_2 (not_2_out, Entrada[4]);
  not not_3 (not_3_out, Entrada[3]);
  not not_4 (not_4_out, Entrada[2]);
  not not_5 (not_5_out, Entrada[5]);
  not not_6 (not_6_out, Entrada[4]);
  not not_7 (not_7_out, Entrada[3]);
  not not_8 (not_8_out, Entrada[2]);
  not not_9 (not_9_out, Entrada[5]);
  not not_10 (not_10_out, Entrada[5]);
  not not_11 (not_11_out, Entrada[5]);
  not not_12 (not_12_out, Entrada[5]);
  not not_13 (not_13_out, Entrada[4]);
  not not_14 (not_14_out, Entrada[5]);
  not not_15 (not_15_out, Entrada[4]);
  not not_16 (not_16_out, Entrada[7]);
  not not_17 (not_17_out, Entrada[6]);
  not not_18 (not_18_out, Entrada[5]);
  not not_19 (not_19_out, Entrada[3]);
  not not_20 (not_20_out, Entrada[1]);
  not not_21 (not_21_out, Entrada[5]);
  not not_22 (not_22_out, Entrada[3]);
  not not_23 (not_23_out, Entrada[5]);
  not not_24 (not_24_out, Entrada[6]);
  and and_1 (and_1_out, not_1_out, not_2_out, not_3_out, not_4_out, Entrada[0]);
  and and_2 (and_2_out, not_5_out, not_6_out, not_7_out, not_8_out, Entrada[1]);
  and and_3 (and_3_out, not_9_out, Entrada[2]);
  and and_4 (and_4_out, not_10_out, Entrada[3]);
  and and_5 (and_5_out, not_11_out, Entrada[4]);
  and and_6 (and_6_out, Entrada[7], Entrada[6], Entrada[5]);
  and and_7 (and_7_out, not_12_out, not_13_out, Entrada[2]);
  and and_8 (and_8_out, not_14_out, not_15_out, Entrada[3]);
  and and_9 (and_9_out, not_16_out, Entrada[6], Entrada[5]);
  and and_10 (and_10_out, Entrada[7], not_17_out, Entrada[5]);
  and and_11 (and_11_out, not_18_out, not_19_out, not_20_out, Entrada[0]);
  and and_12 (and_12_out, not_21_out, not_22_out, Entrada[2]);
  and and_13 (and_13_out, not_23_out, Entrada[4]);
  and and_14 (and_14_out, not_24_out, Entrada[5]);
  or or_1 (Direccion[3], and_1_out, and_2_out);
  or or_2 (Direccion[2], and_3_out, and_4_out, and_5_out, and_6_out);
  or or_3 (Direccion[1], and_7_out, and_8_out, and_9_out, and_10_out);
  or or_4 (Direccion[0], and_11_out, and_12_out, and_13_out, and_14_out);
endmodule

module HazardDetectionUnit (
  input  ID_EX_MemRead,
  input  [4:0] ID_EX_rt,
  input  [4:0] IF_ID_rs,
  input  [4:0] IF_ID_rt,
  output stall,
  output enablePC
);

  wire comparator_1_eq, comparator_2_eq, or_1_out;

  Comparator #(.width(5)) comparator_1 (.a(ID_EX_rt), .b(IF_ID_rs), .eq(comparator_1_eq));  // open: gt, lt
  Comparator #(.width(5)) comparator_2 (.a(IF_ID_rt), .b(ID_EX_rt), .eq(comparator_2_eq));  // open: gt, lt
  and and_1 (stall, ID_EX_MemRead, or_1_out);
  or or_1 (or_1_out, comparator_1_eq, comparator_2_eq);
  not not_1 (enablePC, stall);
endmodule

module EX_Hazard (
  input  Ex_mem__RegWrite,
  input  [4:0] Ex_Mem__rd,
  input  [4:0] ID_Ex__rs,
  input  [4:0] ID_EX__rt,
  output Stall
);

  wire and_1_out, and_2_out, comparator_1_eq, comparator_2_eq, comparator_3_eq, not_1_out;

  Comparator #(.width(5)) comparator_1 (.a({5{1'b0}}), .b(Ex_Mem__rd), .eq(comparator_1_eq));  // open: gt, lt
  Comparator #(.width(5)) comparator_2 (.a(Ex_Mem__rd), .b(ID_Ex__rs), .eq(comparator_2_eq));  // open: gt, lt
  not not_1 (not_1_out, comparator_1_eq);
  Comparator #(.width(5)) comparator_3 (.a(Ex_Mem__rd), .b(ID_EX__rt), .eq(comparator_3_eq));  // open: gt, lt
  and and_1 (and_1_out, Ex_mem__RegWrite, not_1_out, comparator_2_eq);
  and and_2 (and_2_out, Ex_mem__RegWrite, not_1_out, comparator_3_eq);
  or or_1 (Stall, and_1_out, and_2_out);
endmodule

// signalPC
module Memory_Hazard (
  input  Mem_wb__RegWrite,
  input  [4:0] Mem_wb__rd,
  input  [4:0] Ex_Mem__rd,
  input  [4:0] ID_EX__rs,
  input  [4:0] ID_EX__rt,
  output Stall
);

  wire and_1_out, and_2_out, comparator_1_eq, comparator_2_eq, comparator_3_eq, comparator_4_eq,
       comparator_5_eq, comparator_6_eq, not_1_out, not_2_out, not_3_out, not_4_out;

  not not_1 (not_1_out, comparator_1_eq);
  Comparator #(.width(5)) comparator_1 (.a(Mem_wb__rd), .b({5{1'b0}}), .eq(comparator_1_eq));  // open: gt, lt
  not not_2 (not_2_out, comparator_2_eq);
  Comparator #(.width(5)) comparator_2 (.a(Ex_Mem__rd), .b(ID_EX__rt), .eq(comparator_2_eq));  // open: gt, lt
  Comparator #(.width(5)) comparator_3 (.a(Mem_wb__rd), .b(ID_EX__rt), .eq(comparator_3_eq));  // open: gt, lt
  not not_3 (not_3_out, comparator_4_eq);
  Comparator #(.width(5)) comparator_4 (.a(Mem_wb__rd), .b({5{1'b0}}), .eq(comparator_4_eq));  // open: gt, lt
  not not_4 (not_4_out, comparator_5_eq);
  Comparator #(.width(5)) comparator_5 (.a(Ex_Mem__rd), .b(ID_EX__rs), .eq(comparator_5_eq));  // open: gt, lt
  Comparator #(.width(5)) comparator_6 (.a(Mem_wb__rd), .b(ID_EX__rs), .eq(comparator_6_eq));  // open: gt, lt
  and and_1 (and_1_out, Mem_wb__RegWrite, not_3_out, not_4_out, comparator_6_eq);
  and and_2 (and_2_out, Mem_wb__RegWrite, not_1_out, not_2_out, comparator_3_eq);
  or or_1 (Stall, and_1_out, and_2_out);
endmodule

// Hazard Control
module Hazardv2 (
  input  [31:0] IF_ID__instr,
  input  [31:0] ID_EX__instr,
  input  [4:0] IF_ID__rt,
  input  [4:0] IF_ID__rd,
  input  [4:0] ID_Ex__rt_rd,
  input  Clk,
  input  reset,
  input  [4:0] Mem_Wb__rt_rd,
  input  [31:0] Mem_WB_instr,
  output Stall,
  output SignalPC
);

  wire and_1_out, and_2_out, comparator_1_eq, comparator_2_eq, comparator_3_eq, comparator_4_eq,
       comparator_5_eq, comparator_6_eq, not_1_out, or_1_out, or_2_out;

  Comparator #(.width(5)) comparator_1 (.a(IF_ID__rt), .b(ID_Ex__rt_rd), .eq(comparator_1_eq));  // open: gt, lt
  Comparator #(.width(5)) comparator_2 (.a(IF_ID__rd), .b(ID_Ex__rt_rd), .eq(comparator_2_eq));  // open: gt, lt
  Comparator #(.width(5)) comparator_3 (.a(IF_ID__rt), .b(Mem_Wb__rt_rd), .eq(comparator_3_eq));  // open: gt, lt
  Comparator #(.width(5)) comparator_4 (.a(Mem_Wb__rt_rd), .b(IF_ID__rd), .eq(comparator_4_eq));  // open: gt, lt
  // Probe on IF_ID__instr
  // Probe on ID_EX__instr
  // Probe on Mem_WB_instr
  Comparator #(.width(32)) comparator_5 (.a(IF_ID__instr), .b(ID_EX__instr), .eq(comparator_5_eq));  // open: gt, lt
  not not_1 (not_1_out, comparator_5_eq);
  or or_1 (or_1_out, comparator_1_eq, comparator_2_eq);
  or or_2 (or_2_out, comparator_3_eq, comparator_4_eq);
  Comparator #(.width(32)) comparator_6 (.a(Mem_WB_instr), .b({32{1'b0}}), .eq(comparator_6_eq));  // open: gt, lt
  and and_1 (and_1_out, not_1_out, or_1_out);
  and and_2 (and_2_out, or_2_out, comparator_6_eq);
  S_R_Flip_Flop #(.trigger("high")) s_r_ff_1 (
    .S(and_1_out), .clk(Clk), .R(and_2_out), .Q(Stall), .reset(reset));  // open: Qn, preset, en
  not not_2 (SignalPC, Stall);
endmodule

module Forward_Unit (
  input  EX_MEM__RegWrite,
  input  [4:0] EX_MEM__Rd,
  input  [4:0] ID_EX__rs,
  input  [4:0] ID_EX__rt,
  input  MEM_WB___RegWrite,
  input  [4:0] MEM_WB_rd,
  input  EX_MEM__memWrite,
  output [1:0] ForwardA,
  output [1:0] ForwardB,
  output memForward
);

  wire and_1_out, and_2_out, and_3_out, and_4_out, comparator_1_eq, comparator_2_eq, comparator_3_eq,
       comparator_4_eq, comparator_5_eq, comparator_6_eq, comparator_7_eq, not_1_out, not_2_out, not_3_out,
       not_4_out;

  Comparator #(.width(5)) comparator_1 (.a(EX_MEM__Rd), .b({5{1'b0}}), .eq(comparator_1_eq));  // open: gt, lt
  Comparator #(.width(5)) comparator_2 (.a(ID_EX__rs), .b(EX_MEM__Rd), .eq(comparator_2_eq));  // open: gt, lt
  Comparator #(.width(5)) comparator_3 (.a(ID_EX__rt), .b(EX_MEM__Rd), .eq(comparator_3_eq));  // open: gt, lt
  Comparator #(.width(5)) comparator_4 (.a(MEM_WB_rd), .b({5{1'b0}}), .eq(comparator_4_eq));  // open: gt, lt
  Comparator #(.width(5)) comparator_5 (.a(ID_EX__rs), .b(MEM_WB_rd), .eq(comparator_5_eq));  // open: gt, lt
  Comparator #(.width(5)) comparator_6 (.a(ID_EX__rt), .b(MEM_WB_rd), .eq(comparator_6_eq));  // open: gt, lt
  Comparator #(.width(5)) comparator_7 (.a(EX_MEM__Rd), .b(MEM_WB_rd), .eq(comparator_7_eq));  // open: gt, lt
  not not_1 (not_1_out, comparator_1_eq);
  not not_2 (not_2_out, comparator_4_eq);
  and and_1 (and_1_out, EX_MEM__RegWrite, not_1_out);
  and and_2 (and_2_out, MEM_WB___RegWrite, not_2_out);
  and and_3 (and_3_out, and_2_out, comparator_5_eq);
  and and_4 (and_4_out, and_2_out, comparator_6_eq);
  and and_5 (memForward, MEM_WB___RegWrite, comparator_7_eq, not_2_out, EX_MEM__memWrite);
  and and_6 (ForwardA[1], and_1_out, comparator_2_eq);
  and and_7 (ForwardB[1], and_1_out, comparator_3_eq);
  not not_3 (not_3_out, ForwardA[1]);
  not not_4 (not_4_out, ForwardB[1]);
  and and_8 (ForwardA[0], and_3_out, not_3_out);
  and and_9 (ForwardB[0], and_4_out, not_4_out);

  // Other names for the same wires on the sheet: ForwardMemA = ForwardA[0]; ForwardExA = ForwardA[1];
  //   ForwardMemB = ForwardB[0]; ForwardExB = ForwardB[1]
endmodule

// Hazard
module HazardWithForward (
  input  ID_EX__MemRead,
  input  [4:0] ID_EX__rt,
  input  [4:0] IF_ID__rs,
  input  [4:0] IF_ID__rt,
  input  lw_instruction,
  output IF_ID__stall,
  output PC_enable,
  output Stall_Control
);

  wire and_1_out, comparator_1_eq, comparator_2_eq, not_1_out, or_1_out;

  not not_1 (not_1_out, lw_instruction);
  Comparator #(.width(5)) comparator_1 (.a(ID_EX__rt), .b(IF_ID__rs), .eq(comparator_1_eq));  // open: gt, lt
  Comparator #(.width(5)) comparator_2 (.a(ID_EX__rt), .b(IF_ID__rt), .eq(comparator_2_eq));  // open: gt, lt
  and and_1 (and_1_out, comparator_2_eq, not_1_out);
  and and_2 (Stall_Control, ID_EX__MemRead, or_1_out);
  or or_1 (or_1_out, comparator_1_eq, and_1_out);
  not not_2 (IF_ID__stall, Stall_Control);

  assign PC_enable = IF_ID__stall;
endmodule
